// Logisim project P0_L0_CRC.circ as structural Verilog: 2 circuits, main circuit CRC
module CRC (
  input  [7:0] in_1,
  input  [3:0] in_2,
  output [10:0] out_3
);

  wire [2:0] n4_bit_1_out_3, n4_bit_2_out_3, n4_bit_3_out_3, n4_bit_4_out_3, n4_bit_5_out_3, n4_bit_6_out_3,
       n4_bit_7_out_3;

  // Probe on in_1[7:4]
  _4_BIT u_4_bit_1 (.in_1(in_1[7:4]), .in_2(in_2), .out_3(n4_bit_1_out_3));  // open: out_4
  // Probe on n4_bit_1_out_3
  _4_BIT u_4_bit_2 (.in_1({n4_bit_3_out_3, in_1[2]}), .in_2(in_2), .out_3(n4_bit_2_out_3));  // open: out_4
  _4_BIT u_4_bit_3 (.in_1({n4_bit_1_out_3, in_1[3]}), .in_2(in_2), .out_3(n4_bit_3_out_3));  // open: out_4
  // Probe on n4_bit_3_out_3
  _4_BIT u_4_bit_4 (.in_1({n4_bit_2_out_3, in_1[1]}), .in_2(in_2), .out_3(n4_bit_4_out_3));  // open: out_4
  _4_BIT u_4_bit_5 (.in_1({n4_bit_4_out_3, in_1[0]}), .in_2(in_2), .out_3(n4_bit_5_out_3));  // open: out_4
  _4_BIT u_4_bit_6 (.in_1({n4_bit_5_out_3, 1'b0}), .in_2(in_2), .out_3(n4_bit_6_out_3));  // open: out_4
  _4_BIT u_4_bit_7 (.in_1({n4_bit_6_out_3, 1'b0}), .in_2(in_2), .out_3(n4_bit_7_out_3));  // open: out_4
  _4_BIT u_4_bit_8 (.in_1({n4_bit_7_out_3, 1'b0}), .in_2(in_2), .out_3(out_3[2:0]));  // open: out_4

  assign out_3[10:3] = in_1;
endmodule

module _4_BIT (
  input  [3:0] in_1,
  input  [3:0] in_2,
  output [2:0] out_3,
  output out_4
);

  wire not_1_out;
  wire [2:0] bit_extender_1_out;
  wire [3:0] xor_1_out;

  assign xor_1_out = in_1 ^ in_2;  // XOR_Gate xor_1, 4 bits wide
  Bit_Extender #(.in_width(4), .out_width(3)) bit_extender_1 (.in(xor_1_out), .out(bit_extender_1_out));
  Multiplexer #(.width(3)) multiplexer_1 (
    .in0(bit_extender_1_out), .in1(in_1[2:0]), .out(out_3), .sel(not_1_out));  // open: en
  not not_1 (not_1_out, in_1[3]);

  assign out_4 = in_1[3];
endmodule
