// Logisim project P0_L0_FSM.circ as structural Verilog: 3 circuits, main circuit fsm
module fsm (
  input  in_1,
  input  [1:0] in_2,
  output out_3
);

  wire clk, counter_1_q;
  wire [1:0] in_1_out_3, multiplexer_1_out, multiplexer_2_out, or_1_out, register_1_q;

  Clock clock_1 (.out(clk));
  // Probe on register_1_q
  Multiplexer #(.width(2)) multiplexer_1 (
    .in0(2'b00), .in1(2'b00), .out(multiplexer_1_out), .sel(counter_1_q));  // open: en
  Counter #(.width(1), .max('h1), .ongoal("stay")) counter_1 (
    .Q(counter_1_q), .clk(clk));  // open: load, D, count, carry, clr
  // Probe on in_1_out_3
  // Probe on in_1_out_3
  assign or_1_out = register_1_q | multiplexer_1_out;  // OR_Gate or_1, 2 bits wide
  in u_in_1 (.in_1(or_1_out), .in_2(in_2), .out_3(in_1_out_3));
  // Probe on register_1_q
  Multiplexer #(.width(2)) multiplexer_2 (
    .in0(in_1_out_3), .in1(2'b00), .out(multiplexer_2_out), .sel(in_1));  // open: en
  Register #(.width(2)) register_1 (.D(multiplexer_2_out), .Q(register_1_q), .clk(clk));  // open: en, clr
  out out_1 (.in_1(register_1_q), .in_2(in_2), .Z(out_3));

  // Other names for the same wires on the sheet: clr = in_1; in[1:0] = in_2; Z = out_3
endmodule

module in (
  input  [1:0] in_1,
  input  [1:0] in_2,
  output [1:0] out_3
);

  wire and_1_out, and_2_out, and_3_out, and_4_out, not_1_out, not_2_out, not_3_out, not_4_out, not_5_out,
       not_6_out, not_7_out;

  not not_1 (not_1_out, in_1[1]);
  and and_1 (and_1_out, not_1_out, in_1[0], not_2_out);
  not not_2 (not_2_out, in_2[0]);
  not not_3 (not_3_out, in_1[0]);
  and and_2 (and_2_out, in_1[1], not_3_out, not_4_out);
  not not_4 (not_4_out, in_2[0]);
  not not_5 (not_5_out, in_2[1]);
  and and_3 (and_3_out, not_5_out, in_2[0]);
  not not_6 (not_6_out, in_1[0]);
  and and_4 (and_4_out, in_1[1], not_6_out, not_7_out);
  not not_7 (not_7_out, in_2[0]);
  or or_1 (out_3[1], and_1_out, and_2_out);
  or or_2 (out_3[0], and_3_out, and_4_out);
endmodule

module out (
  input  [1:0] in_1,
  input  [1:0] in_2,
  output Z
);

  wire not_1_out, not_2_out;

  not not_1 (not_1_out, in_1[0]);
  not not_2 (not_2_out, in_2[0]);
  and and_1 (Z, in_1[1], not_1_out, not_2_out);
endmodule
