// Logisim project P0_L0_GRF.circ as structural Verilog: 3 circuits, main circuit grf
module grf (
  input  in_1,
  input  in_2,
  input  in_3,
  input  [4:0] in_4,
  input  [4:0] in_5,
  input  [4:0] in_6,
  input  [31:0] in_7,
  output [31:0] out_8,
  output [31:0] out_9
);

  wire in_1_out_36, in_1_out_37, in_1_out_38, in_1_out_39, in_1_out_40, in_1_out_41, in_1_out_42,
       in_1_out_43, in_1_out_44, in_1_out_45, in_1_out_46, in_1_out_47, in_1_out_48, in_1_out_49,
       in_1_out_50, in_1_out_51, in_1_out_52, in_1_out_53, in_1_out_54, in_1_out_55, in_1_out_56,
       in_1_out_57, in_1_out_58, in_1_out_59, in_1_out_60, in_1_out_61, in_1_out_62, in_1_out_63,
       in_1_out_64, in_1_out_65, in_1_out_66, in_1_out_67;
  wire [31:0] in_1_out_4, in_1_out_5, in_1_out_6, in_1_out_7, in_1_out_8, in_1_out_9, in_1_out_10,
       in_1_out_11, in_1_out_12, in_1_out_13, in_1_out_14, in_1_out_15, in_1_out_16, in_1_out_17,
       in_1_out_18, in_1_out_19, in_1_out_20, in_1_out_21, in_1_out_22, in_1_out_23, in_1_out_24,
       in_1_out_25, in_1_out_26, in_1_out_27, in_1_out_28, in_1_out_29, in_1_out_30, in_1_out_31,
       in_1_out_32, in_1_out_33, in_1_out_34, in_1_out_35, n32_rigister_1_out_67, n32_rigister_1_out_68,
       n32_rigister_1_out_69, n32_rigister_1_out_70, n32_rigister_1_out_71, n32_rigister_1_out_72,
       n32_rigister_1_out_73, n32_rigister_1_out_74, n32_rigister_1_out_75, n32_rigister_1_out_76,
       n32_rigister_1_out_77, n32_rigister_1_out_78, n32_rigister_1_out_79, n32_rigister_1_out_80,
       n32_rigister_1_out_81, n32_rigister_1_out_82, n32_rigister_1_out_83, n32_rigister_1_out_84,
       n32_rigister_1_out_85, n32_rigister_1_out_86, n32_rigister_1_out_87, n32_rigister_1_out_88,
       n32_rigister_1_out_89, n32_rigister_1_out_90, n32_rigister_1_out_91, n32_rigister_1_out_92,
       n32_rigister_1_out_93, n32_rigister_1_out_94, n32_rigister_1_out_95, n32_rigister_1_out_96,
       n32_rigister_1_out_97, n32_rigister_1_out_98;

  in u_in_1 (
    .in_2(in_7), .in_3(in_6), .in_1(in_3), .out_4(in_1_out_4), .out_5(in_1_out_5), .out_6(in_1_out_6),
    .out_7(in_1_out_7), .out_8(in_1_out_8), .out_9(in_1_out_9), .out_10(in_1_out_10), .out_11(in_1_out_11),
    .out_12(in_1_out_12), .out_13(in_1_out_13), .out_14(in_1_out_14), .out_15(in_1_out_15),
    .out_16(in_1_out_16), .out_17(in_1_out_17), .out_18(in_1_out_18), .out_19(in_1_out_19),
    .out_20(in_1_out_20), .out_21(in_1_out_21), .out_22(in_1_out_22), .out_23(in_1_out_23),
    .out_24(in_1_out_24), .out_25(in_1_out_25), .out_26(in_1_out_26), .out_27(in_1_out_27),
    .out_28(in_1_out_28), .out_29(in_1_out_29), .out_30(in_1_out_30), .out_31(in_1_out_31),
    .out_32(in_1_out_32), .out_33(in_1_out_33), .out_34(in_1_out_34), .out_35(in_1_out_35),
    .out_36(in_1_out_36), .out_37(in_1_out_37), .out_38(in_1_out_38), .out_39(in_1_out_39),
    .out_40(in_1_out_40), .out_41(in_1_out_41), .out_42(in_1_out_42), .out_43(in_1_out_43),
    .out_44(in_1_out_44), .out_45(in_1_out_45), .out_46(in_1_out_46), .out_47(in_1_out_47),
    .out_48(in_1_out_48), .out_49(in_1_out_49), .out_50(in_1_out_50), .out_51(in_1_out_51),
    .out_52(in_1_out_52), .out_53(in_1_out_53), .out_54(in_1_out_54), .out_55(in_1_out_55),
    .out_56(in_1_out_56), .out_57(in_1_out_57), .out_58(in_1_out_58), .out_59(in_1_out_59),
    .out_60(in_1_out_60), .out_61(in_1_out_61), .out_62(in_1_out_62), .out_63(in_1_out_63),
    .out_64(in_1_out_64), .out_65(in_1_out_65), .out_66(in_1_out_66), .out_67(in_1_out_67));
  _32_rigister u_32_rigister_1 (
    ._1(in_1_out_4), ._2(in_1_out_5), ._3(in_1_out_6), ._4(in_1_out_7), ._1_2(in_1_out_8), ._2_2(in_1_out_9),
    ._3_2(in_1_out_10), ._4_2(in_1_out_11), ._1_3(in_1_out_12), ._2_3(in_1_out_13), ._3_3(in_1_out_14),
    ._4_3(in_1_out_15), ._1_4(in_1_out_16), ._2_4(in_1_out_17), ._3_4(in_1_out_18), ._4_4(in_1_out_19),
    ._1_5(in_1_out_20), ._2_5(in_1_out_21), ._3_5(in_1_out_22), ._4_5(in_1_out_23), ._1_6(in_1_out_24),
    ._2_6(in_1_out_25), ._3_6(in_1_out_26), ._4_6(in_1_out_27), ._1_7(in_1_out_28), ._2_7(in_1_out_29),
    ._3_7(in_1_out_30), ._4_7(in_1_out_31), ._1_8(in_1_out_32), ._2_8(in_1_out_33), ._3_8(in_1_out_34),
    ._4_8(in_1_out_35), .in_1(in_1), .in_2(in_2), .en1(in_1_out_36), .en2(in_1_out_37), .en3(in_1_out_38),
    .en4(in_1_out_39), .en1_2(in_1_out_40), .en2_2(in_1_out_41), .en3_2(in_1_out_42), .en4_2(in_1_out_43),
    .en1_3(in_1_out_44), .en2_3(in_1_out_45), .en3_3(in_1_out_46), .en4_3(in_1_out_47), .en1_4(in_1_out_48),
    .en2_4(in_1_out_49), .en3_4(in_1_out_50), .en4_4(in_1_out_51), .en1_5(in_1_out_52), .en2_5(in_1_out_53),
    .en3_5(in_1_out_54), .en4_5(in_1_out_55), .en1_6(in_1_out_56), .en2_6(in_1_out_57), .en3_6(in_1_out_58),
    .en4_6(in_1_out_59), .en1_7(in_1_out_60), .en2_7(in_1_out_61), .en3_7(in_1_out_62), .en4_7(in_1_out_63),
    .en1_8(in_1_out_64), .en2_8(in_1_out_65), .en3_8(in_1_out_66), .en4_8(in_1_out_67),
    .out_67(n32_rigister_1_out_67), .out_68(n32_rigister_1_out_68), .out_69(n32_rigister_1_out_69),
    .out_70(n32_rigister_1_out_70), .out_71(n32_rigister_1_out_71), .out_72(n32_rigister_1_out_72),
    .out_73(n32_rigister_1_out_73), .out_74(n32_rigister_1_out_74), .out_75(n32_rigister_1_out_75),
    .out_76(n32_rigister_1_out_76), .out_77(n32_rigister_1_out_77), .out_78(n32_rigister_1_out_78),
    .out_79(n32_rigister_1_out_79), .out_80(n32_rigister_1_out_80), .out_81(n32_rigister_1_out_81),
    .out_82(n32_rigister_1_out_82), .out_83(n32_rigister_1_out_83), .out_84(n32_rigister_1_out_84),
    .out_85(n32_rigister_1_out_85), .out_86(n32_rigister_1_out_86), .out_87(n32_rigister_1_out_87),
    .out_88(n32_rigister_1_out_88), .out_89(n32_rigister_1_out_89), .out_90(n32_rigister_1_out_90),
    .out_91(n32_rigister_1_out_91), .out_92(n32_rigister_1_out_92), .out_93(n32_rigister_1_out_93),
    .out_94(n32_rigister_1_out_94), .out_95(n32_rigister_1_out_95), .out_96(n32_rigister_1_out_96),
    .out_97(n32_rigister_1_out_97), .out_98(n32_rigister_1_out_98));
  Multiplexer #(.select(5), .width(32), .enable("false")) multiplexer_1 (
    .in0(n32_rigister_1_out_67), .in1(n32_rigister_1_out_68), .in2(n32_rigister_1_out_69),
    .in3(n32_rigister_1_out_70), .in4(n32_rigister_1_out_71), .in5(n32_rigister_1_out_72),
    .in6(n32_rigister_1_out_73), .in7(n32_rigister_1_out_74), .in8(n32_rigister_1_out_75),
    .in9(n32_rigister_1_out_76), .in10(n32_rigister_1_out_77), .in11(n32_rigister_1_out_78),
    .in12(n32_rigister_1_out_79), .in13(n32_rigister_1_out_80), .in14(n32_rigister_1_out_81),
    .in15(n32_rigister_1_out_82), .in16(n32_rigister_1_out_83), .in17(n32_rigister_1_out_84),
    .in18(n32_rigister_1_out_85), .in19(n32_rigister_1_out_86), .in20(n32_rigister_1_out_87),
    .in21(n32_rigister_1_out_88), .in22(n32_rigister_1_out_89), .in23(n32_rigister_1_out_90),
    .in24(n32_rigister_1_out_91), .in25(n32_rigister_1_out_92), .in26(n32_rigister_1_out_93),
    .in27(n32_rigister_1_out_94), .in28(n32_rigister_1_out_95), .in29(n32_rigister_1_out_96),
    .in30(n32_rigister_1_out_97), .in31(n32_rigister_1_out_98), .out(out_8), .sel(in_4));
  Multiplexer #(.select(5), .width(32), .enable("false")) multiplexer_2 (
    .in0(n32_rigister_1_out_67), .in1(n32_rigister_1_out_68), .in2(n32_rigister_1_out_69),
    .in3(n32_rigister_1_out_70), .in4(n32_rigister_1_out_71), .in5(n32_rigister_1_out_72),
    .in6(n32_rigister_1_out_73), .in7(n32_rigister_1_out_74), .in8(n32_rigister_1_out_75),
    .in9(n32_rigister_1_out_76), .in10(n32_rigister_1_out_77), .in11(n32_rigister_1_out_78),
    .in12(n32_rigister_1_out_79), .in13(n32_rigister_1_out_80), .in14(n32_rigister_1_out_81),
    .in15(n32_rigister_1_out_82), .in16(n32_rigister_1_out_83), .in17(n32_rigister_1_out_84),
    .in18(n32_rigister_1_out_85), .in19(n32_rigister_1_out_86), .in20(n32_rigister_1_out_87),
    .in21(n32_rigister_1_out_88), .in22(n32_rigister_1_out_89), .in23(n32_rigister_1_out_90),
    .in24(n32_rigister_1_out_91), .in25(n32_rigister_1_out_92), .in26(n32_rigister_1_out_93),
    .in27(n32_rigister_1_out_94), .in28(n32_rigister_1_out_95), .in29(n32_rigister_1_out_96),
    .in30(n32_rigister_1_out_97), .in31(n32_rigister_1_out_98), .out(out_9), .sel(in_5));

  // Other names for the same wires on the sheet: A1[4:0] = in_4; A2[4:0] = in_5; A3[4:0] = in_6; clk = in_1;
  //   en = in_3; reset = in_2; WD[31:0] = in_7
endmodule

module _32_rigister (
  input  in_1,
  input  in_2,
  input  [31:0] _1,
  input  en1,
  input  [31:0] _2,
  input  en2,
  input  [31:0] _3,
  input  en3,
  input  [31:0] _4,
  input  en4,
  input  [31:0] _1_2,
  input  en1_2,
  input  [31:0] _2_2,
  input  en2_2,
  input  [31:0] _3_2,
  input  en3_2,
  input  [31:0] _4_2,
  input  en4_2,
  input  [31:0] _1_3,
  input  en1_3,
  input  [31:0] _2_3,
  input  en2_3,
  input  [31:0] _3_3,
  input  en3_3,
  input  [31:0] _4_3,
  input  en4_3,
  input  [31:0] _1_4,
  input  en1_4,
  input  [31:0] _2_4,
  input  en2_4,
  input  [31:0] _3_4,
  input  en3_4,
  input  [31:0] _4_4,
  input  en4_4,
  input  [31:0] _1_5,
  input  en1_5,
  input  [31:0] _2_5,
  input  en2_5,
  input  [31:0] _3_5,
  input  en3_5,
  input  [31:0] _4_5,
  input  en4_5,
  input  [31:0] _1_6,
  input  en1_6,
  input  [31:0] _2_6,
  input  en2_6,
  input  [31:0] _3_6,
  input  en3_6,
  input  [31:0] _4_6,
  input  en4_6,
  input  [31:0] _1_7,
  input  en1_7,
  input  [31:0] _2_7,
  input  en2_7,
  input  [31:0] _3_7,
  input  en3_7,
  input  [31:0] _4_7,
  input  en4_7,
  input  [31:0] _1_8,
  input  en1_8,
  input  [31:0] _2_8,
  input  en2_8,
  input  [31:0] _3_8,
  input  en3_8,
  input  [31:0] _4_8,
  input  en4_8,
  output [31:0] out_67,
  output [31:0] out_68,
  output [31:0] out_69,
  output [31:0] out_70,
  output [31:0] out_71,
  output [31:0] out_72,
  output [31:0] out_73,
  output [31:0] out_74,
  output [31:0] out_75,
  output [31:0] out_76,
  output [31:0] out_77,
  output [31:0] out_78,
  output [31:0] out_79,
  output [31:0] out_80,
  output [31:0] out_81,
  output [31:0] out_82,
  output [31:0] out_83,
  output [31:0] out_84,
  output [31:0] out_85,
  output [31:0] out_86,
  output [31:0] out_87,
  output [31:0] out_88,
  output [31:0] out_89,
  output [31:0] out_90,
  output [31:0] out_91,
  output [31:0] out_92,
  output [31:0] out_93,
  output [31:0] out_94,
  output [31:0] out_95,
  output [31:0] out_96,
  output [31:0] out_97,
  output [31:0] out_98
);

  Register #(.width(32)) register_1 (.D(_1), .en(1'b0), .Q(out_67), .clk(in_1), .clr(in_2));
  Register #(.width(32)) register_2 (.D(_2), .en(en2), .Q(out_68), .clk(in_1), .clr(in_2));
  Register #(.width(32)) register_3 (.D(_3), .en(en3), .Q(out_69), .clk(in_1), .clr(in_2));
  Register #(.width(32)) register_4 (.D(_4), .en(en4), .Q(out_70), .clk(in_1), .clr(in_2));
  Register #(.width(32)) register_5 (.D(_1_2), .en(en1_2), .Q(out_71), .clk(in_1), .clr(in_2));
  Register #(.width(32)) register_6 (.D(_2_2), .en(en2_2), .Q(out_72), .clk(in_1), .clr(in_2));
  Register #(.width(32)) register_7 (.D(_3_2), .en(en3_2), .Q(out_73), .clk(in_1), .clr(in_2));
  Register #(.width(32)) register_8 (.D(_4_2), .en(en4_2), .Q(out_74), .clk(in_1), .clr(in_2));
  Register #(.width(32)) register_9 (.D(_1_3), .en(en1_3), .Q(out_75), .clk(in_1), .clr(in_2));
  Register #(.width(32)) register_10 (.D(_2_3), .en(en2_3), .Q(out_76), .clk(in_1), .clr(in_2));
  Register #(.width(32)) register_11 (.D(_3_3), .en(en3_3), .Q(out_77), .clk(in_1), .clr(in_2));
  Register #(.width(32)) register_12 (.D(_4_3), .en(en4_3), .Q(out_78), .clk(in_1), .clr(in_2));
  Register #(.width(32)) register_13 (.D(_1_4), .en(en1_4), .Q(out_79), .clk(in_1), .clr(in_2));
  Register #(.width(32)) register_14 (.D(_2_4), .en(en2_4), .Q(out_80), .clk(in_1), .clr(in_2));
  Register #(.width(32)) register_15 (.D(_3_4), .en(en3_4), .Q(out_81), .clk(in_1), .clr(in_2));
  Register #(.width(32)) register_16 (.D(_4_4), .en(en4_4), .Q(out_82), .clk(in_1), .clr(in_2));
  Register #(.width(32)) register_17 (.D(_1_5), .en(en1_5), .Q(out_83), .clk(in_1), .clr(in_2));
  Register #(.width(32)) register_18 (.D(_2_5), .en(en2_5), .Q(out_84), .clk(in_1), .clr(in_2));
  Register #(.width(32)) register_19 (.D(_3_5), .en(en3_5), .Q(out_85), .clk(in_1), .clr(in_2));
  Register #(.width(32)) register_20 (.D(_4_5), .en(en4_5), .Q(out_86), .clk(in_1), .clr(in_2));
  Register #(.width(32)) register_21 (.D(_1_6), .en(en1_6), .Q(out_87), .clk(in_1), .clr(in_2));
  Register #(.width(32)) register_22 (.D(_2_6), .en(en2_6), .Q(out_88), .clk(in_1), .clr(in_2));
  Register #(.width(32)) register_23 (.D(_3_6), .en(en3_6), .Q(out_89), .clk(in_1), .clr(in_2));
  Register #(.width(32)) register_24 (.D(_4_6), .en(en4_6), .Q(out_90), .clk(in_1), .clr(in_2));
  Register #(.width(32)) register_25 (.D(_1_7), .en(en1_7), .Q(out_91), .clk(in_1), .clr(in_2));
  Register #(.width(32)) register_26 (.D(_2_7), .en(en2_7), .Q(out_92), .clk(in_1), .clr(in_2));
  Register #(.width(32)) register_27 (.D(_3_7), .en(en3_7), .Q(out_93), .clk(in_1), .clr(in_2));
  Register #(.width(32)) register_28 (.D(_4_7), .en(en4_7), .Q(out_94), .clk(in_1), .clr(in_2));
  Register #(.width(32)) register_29 (.D(_1_8), .en(en1_8), .Q(out_95), .clk(in_1), .clr(in_2));
  Register #(.width(32)) register_30 (.D(_2_8), .en(en2_8), .Q(out_96), .clk(in_1), .clr(in_2));
  Register #(.width(32)) register_31 (.D(_3_8), .en(en3_8), .Q(out_97), .clk(in_1), .clr(in_2));
  Register #(.width(32)) register_32 (.D(_4_8), .en(en4_8), .Q(out_98), .clk(in_1), .clr(in_2));

  // Other names for the same wires on the sheet: clk = in_1; reset = in_2
endmodule

module in (
  input  in_1,
  input  [31:0] in_2,
  input  [4:0] in_3,
  output [31:0] out_4,
  output [31:0] out_5,
  output [31:0] out_6,
  output [31:0] out_7,
  output [31:0] out_8,
  output [31:0] out_9,
  output [31:0] out_10,
  output [31:0] out_11,
  output [31:0] out_12,
  output [31:0] out_13,
  output [31:0] out_14,
  output [31:0] out_15,
  output [31:0] out_16,
  output [31:0] out_17,
  output [31:0] out_18,
  output [31:0] out_19,
  output [31:0] out_20,
  output [31:0] out_21,
  output [31:0] out_22,
  output [31:0] out_23,
  output [31:0] out_24,
  output [31:0] out_25,
  output [31:0] out_26,
  output [31:0] out_27,
  output [31:0] out_28,
  output [31:0] out_29,
  output [31:0] out_30,
  output [31:0] out_31,
  output [31:0] out_32,
  output [31:0] out_33,
  output [31:0] out_34,
  output [31:0] out_35,
  output out_36,
  output out_37,
  output out_38,
  output out_39,
  output out_40,
  output out_41,
  output out_42,
  output out_43,
  output out_44,
  output out_45,
  output out_46,
  output out_47,
  output out_48,
  output out_49,
  output out_50,
  output out_51,
  output out_52,
  output out_53,
  output out_54,
  output out_55,
  output out_56,
  output out_57,
  output out_58,
  output out_59,
  output out_60,
  output out_61,
  output out_62,
  output out_63,
  output out_64,
  output out_65,
  output out_66,
  output out_67
);

  Demultiplexer #(.select(5), .width(32)) demultiplexer_1 (
    .out0(out_4), .out1(out_5), .out2(out_6), .out3(out_7), .out4(out_8), .out5(out_9), .out6(out_10),
    .out7(out_11), .out8(out_12), .out9(out_13), .out10(out_14), .out11(out_15), .out12(out_16),
    .out13(out_17), .out14(out_18), .out15(out_19), .out16(out_20), .out17(out_21), .out18(out_22),
    .out19(out_23), .out20(out_24), .out21(out_25), .out22(out_26), .out23(out_27), .out24(out_28),
    .out25(out_29), .out26(out_30), .out27(out_31), .out28(out_32), .out29(out_33), .out30(out_34),
    .out31(out_35), .in(in_2), .sel(in_3), .en(in_1));
  Decoder #(.select(5)) decoder_1 (
    .out0(out_36), .out1(out_37), .out2(out_38), .out3(out_39), .out4(out_40), .out5(out_41), .out6(out_42),
    .out7(out_43), .out8(out_44), .out9(out_45), .out10(out_46), .out11(out_47), .out12(out_48),
    .out13(out_49), .out14(out_50), .out15(out_51), .out16(out_52), .out17(out_53), .out18(out_54),
    .out19(out_55), .out20(out_56), .out21(out_57), .out22(out_58), .out23(out_59), .out24(out_60),
    .out25(out_61), .out26(out_62), .out27(out_63), .out28(out_64), .out29(out_65), .out30(out_66),
    .out31(out_67), .sel(in_3), .en(in_1));

  // Other names for the same wires on the sheet: en = in_1
endmodule
