// Logisim project P0_L1_ftoi.circ as structural Verilog: 1 circuit, main circuit ftoi
module ftoi (
  input  [15:0] in_1,
  output [31:0] out_2
);

  wire comparator_1_eq, comparator_2_eq;
  wire [4:0] bit_extender_3_out;
  wire [5:0] adder_1_out, bit_extender_1_out, subtractor_1_out;
  wire [10:10] decoder_1_out0;
  wire [30:0] adder_2_out, bit_extender_2_out, multiplexer_1_out, shifter_1_out, shifter_2_out,
       subtractor_2_out;
  wire [31:31] decoder_2_out1;

  assign bit_extender_1_out = {{1{1'b0}}, in_1[14:10]};  // Bit_Extender bit_extender_1
  Decoder #(.disabled(0), .enable("false")) decoder_1 (.out0(decoder_1_out0[10]), .sel(comparator_1_eq));  // open: out1
  Comparator #(.width(5)) comparator_1 (.a(in_1[14:10]), .b({5{1'b0}}), .eq(comparator_1_eq));  // open: gt, lt
  Comparator #(.width(5)) comparator_2 (.a(in_1[14:10]), .b({5{1'b1}}), .eq(comparator_2_eq));  // open: gt, lt
  Subtractor #(.width(6)) subtractor_1 (
    .a(6'b010000), .b(bit_extender_1_out), .out(subtractor_1_out));  // open: bin, bout
  // Probe on bit_extender_2_out
  assign bit_extender_2_out = {{20{1'b0}}, {decoder_1_out0[10], in_1[9:0]}};  // Bit_Extender bit_extender_2
  // Probe on subtractor_1_out
  Shifter #(.width(31)) shifter_1 (.in(bit_extender_2_out), .\dist (5'b00110), .out(shifter_1_out));
  Adder #(.width(6)) adder_1 (.a(subtractor_1_out), .b(6'b001111), .out(adder_1_out));  // open: cin, cout
  Bit_Extender #(.in_width(6), .out_width(5)) bit_extender_3 (.in(adder_1_out), .out(bit_extender_3_out));
  // Probe on adder_1_out
  // Probe on adder_2_out
  Decoder #(.disabled(0), .enable("false")) decoder_2 (.out1(decoder_2_out1[31]), .sel(in_1[15]));  // open: out0
  // Probe on shifter_2_out
  Shifter #(.width(31), .shift("lr")) shifter_2 (.in(shifter_1_out), .\dist (bit_extender_3_out), .out(shifter_2_out));
  Adder #(.width(31)) adder_2 (.a(subtractor_2_out), .b(31'h1), .out(adder_2_out));  // open: cin, cout
  Subtractor #(.width(31)) subtractor_2 (.a({31{1'b1}}), .b(shifter_2_out), .out(subtractor_2_out));  // open: bin, bout
  Multiplexer #(.width(31), .enable("false")) multiplexer_1 (
    .in0(shifter_2_out), .in1(adder_2_out), .out(multiplexer_1_out), .sel(in_1[15]));
  Multiplexer #(.width(32)) multiplexer_2 (
    .in0({decoder_2_out1[31], multiplexer_1_out}), .in1({32{1'b0}}), .out(out_2), .sel(comparator_2_eq));  // open: en
endmodule
