// Logisim project P0_L1_navigation_2020.circ as structural Verilog: 3 circuits, main circuit navigation
module navigation (
  input  [1:0] in_1,
  input  in_2,
  input  in_3,
  output out_4,
  output out_5
);

  wire counter_1_q;
  wire [4:0] in_out_3, multiplexer_1_out, or_1_out, register_1_q;

  // Probe on register_1_q
  Counter #(.width(1), .max('h1), .ongoal("stay")) counter_1 (
    .Q(counter_1_q), .clk(in_2), .clr(in_3));  // open: load, D, count, carry
  // Probe on in_out_3
  // Probe on in_out_3
  assign or_1_out = register_1_q | multiplexer_1_out;  // OR_Gate or_1, 5 bits wide
  Multiplexer #(.width(5)) multiplexer_1 (
    .in0(5'b00001), .in1({5{1'b0}}), .out(multiplexer_1_out), .sel(counter_1_q));  // open: en
  in in (.in_1(or_1_out), .in_2(in_1), .out_3(in_out_3));
  Register #(.width(5)) register_1 (.D(in_out_3), .Q(register_1_q), .clk(in_2), .clr(in_3));  // open: en
  // Probe on register_1_q
  out out_1 (.in_1(register_1_q), .in_2(in_out_3), .in_3(in_2), .in_4(in_3), .out_5(out_4), .out_6(out_5));

  // Other names for the same wires on the sheet: arrive = out_4; clk = in_2; dir[1:0] = in_1; hit = out_5;
  //   reset = in_3
endmodule

module in (
  input  [4:0] in_1,
  input  [1:0] in_2,
  output [4:0] out_3
);

  wire and_1_out, and_2_out, and_3_out, and_4_out, and_5_out, and_6_out, and_7_out, and_8_out, and_9_out,
       and_10_out, and_11_out, and_12_out, and_13_out, and_14_out, and_15_out, and_16_out, not_1_out,
       not_2_out, not_3_out, not_4_out, not_5_out, not_6_out, not_7_out, not_8_out, not_9_out, not_10_out,
       not_11_out, not_12_out, not_13_out, not_14_out, not_15_out, not_16_out, not_17_out, not_18_out,
       not_19_out, not_20_out, not_21_out, not_22_out, not_23_out, not_24_out, not_25_out, not_26_out,
       not_27_out, not_28_out, not_29_out, not_30_out, not_31_out, not_32_out, not_33_out, not_34_out,
       not_35_out, not_36_out, not_37_out, not_38_out, not_39_out, not_40_out, not_41_out, not_42_out,
       not_43_out, not_44_out, not_45_out;

  not not_1 (not_1_out, in_1[3]);
  not not_2 (not_2_out, in_1[2]);
  not not_3 (not_3_out, in_1[1]);
  not not_4 (not_4_out, in_2[1]);
  not not_5 (not_5_out, in_2[0]);
  not not_6 (not_6_out, in_1[4]);
  not not_7 (not_7_out, in_1[2]);
  not not_8 (not_8_out, in_1[0]);
  not not_9 (not_9_out, in_2[1]);
  not not_10 (not_10_out, in_2[0]);
  not not_11 (not_11_out, in_1[4]);
  not not_12 (not_12_out, in_1[2]);
  not not_13 (not_13_out, in_1[0]);
  not not_14 (not_14_out, in_2[1]);
  not not_15 (not_15_out, in_2[0]);
  not not_16 (not_16_out, in_1[4]);
  not not_17 (not_17_out, in_1[3]);
  not not_18 (not_18_out, in_1[0]);
  not not_19 (not_19_out, in_2[1]);
  not not_20 (not_20_out, in_1[4]);
  not not_21 (not_21_out, in_1[3]);
  not not_22 (not_22_out, in_1[0]);
  not not_23 (not_23_out, in_2[1]);
  not not_24 (not_24_out, in_1[4]);
  not not_25 (not_25_out, in_1[3]);
  not not_26 (not_26_out, in_1[0]);
  not not_27 (not_27_out, in_1[4]);
  not not_28 (not_28_out, in_1[3]);
  not not_29 (not_29_out, in_1[0]);
  not not_30 (not_30_out, in_1[3]);
  not not_31 (not_31_out, in_1[2]);
  not not_32 (not_32_out, in_1[1]);
  not not_33 (not_33_out, in_1[3]);
  not not_34 (not_34_out, in_1[2]);
  not not_35 (not_35_out, in_1[1]);
  not not_36 (not_36_out, in_1[4]);
  not not_37 (not_37_out, in_2[1]);
  not not_38 (not_38_out, in_2[0]);
  not not_39 (not_39_out, in_1[4]);
  not not_40 (not_40_out, in_2[1]);
  not not_41 (not_41_out, in_2[0]);
  not not_42 (not_42_out, in_2[1]);
  not not_43 (not_43_out, in_2[0]);
  not not_44 (not_44_out, in_2[0]);
  and and_1 (and_1_out, not_30_out, not_31_out, not_32_out, in_1[0], in_2[0]);
  and and_2 (and_2_out, not_33_out, not_34_out, not_35_out, in_1[0], in_2[1]);
  and and_3 (and_3_out, in_1[1], in_2[1], not_45_out);
  not not_45 (not_45_out, in_2[0]);
  and and_4 (and_4_out, not_36_out, in_1[2], not_37_out, not_38_out);
  or or_1 (out_3[4], and_4_out, and_5_out, and_6_out);
  and and_5 (and_5_out, not_39_out, in_1[3], not_40_out, in_2[0]);
  and and_6 (and_6_out, in_1[4], not_1_out, not_2_out, not_3_out, in_1[0], not_4_out, not_5_out);
  and and_7 (and_7_out, not_6_out, not_7_out, in_1[1], not_8_out, not_9_out, not_10_out);
  and and_8 (and_8_out, not_11_out, in_1[3], not_12_out, not_13_out, not_14_out, not_15_out);
  or or_2 (out_3[3], and_7_out, and_8_out, and_9_out);
  and and_9 (and_9_out, in_1[3], in_2[1], in_2[0]);
  and and_10 (and_10_out, not_16_out, not_17_out, in_1[1], not_18_out, not_19_out, in_2[0]);
  and and_11 (and_11_out, not_20_out, not_21_out, in_1[2], not_22_out, not_23_out, in_2[0]);
  or or_3 (out_3[2], and_10_out, and_11_out, and_12_out);
  and and_12 (and_12_out, in_1[2], in_2[1], not_41_out);
  and and_13 (and_13_out, in_1[0], not_42_out, not_43_out);
  and and_14 (and_14_out, not_24_out, not_25_out, in_1[1], not_26_out, in_2[1], in_2[0]);
  and and_15 (and_15_out, not_27_out, not_28_out, in_1[2], not_29_out, in_2[1], in_2[0]);
  and and_16 (and_16_out, in_1[3], in_2[1], not_44_out);
  or or_4 (out_3[0], and_1_out, and_2_out, and_3_out, in_1[4]);
  or or_5 (out_3[1], and_13_out, and_14_out, and_15_out, and_16_out);

  // Other names for the same wires on the sheet: S0 = in_1[0]; S1 = in_1[1]; S2 = in_1[2]; S3 = in_1[3]; S4 = in_1[4];
  //   IN0 = in_2[0]; IN1 = in_2[1]; OUT0 = out_3[0]; OUT1 = out_3[1]; OUT2 = out_3[2]; OUT3 = out_3[3];
  //   OUT4 = out_3[4]
endmodule

module out (
  input  [4:0] in_1,
  input  [4:0] in_2,
  input  in_3,
  input  in_4,
  output out_5,
  output out_6
);

  wire counter_1_q, counter_2_q;
  wire [4:0] multiplexer_1_out, multiplexer_2_out, or_1_out, or_2_out, register_1_q, register_2_q;

  Multiplexer #(.width(5)) multiplexer_1 (
    .in0(5'b00001), .in1({5{1'b0}}), .out(multiplexer_1_out), .sel(counter_1_q));  // open: en
  Counter #(.width(1), .max('h1), .ongoal("stay")) counter_1 (
    .Q(counter_1_q), .clk(in_3), .clr(in_4));  // open: load, D, count, carry
  assign or_1_out = in_1 | multiplexer_1_out;  // OR_Gate or_1, 5 bits wide
  Comparator #(.width(5)) comparator_1 (.a(5'b10000), .b(or_1_out), .eq(out_5));  // open: gt, lt
  Register #(.width(5)) register_1 (.D(or_1_out), .Q(register_1_q), .clk(in_3), .clr(in_4));  // open: en
  Register #(.width(5)) register_2 (.D(in_2), .Q(register_2_q), .clk(in_3), .clr(in_4));  // open: en
  Multiplexer #(.width(5)) multiplexer_2 (
    .in0(5'b00001), .in1({5{1'b0}}), .out(multiplexer_2_out), .sel(counter_2_q));  // open: en
  Counter #(.width(1), .max('h1), .ongoal("stay")) counter_2 (
    .Q(counter_2_q), .clk(in_3), .clr(in_4));  // open: load, D, count, carry
  assign or_2_out = register_1_q | multiplexer_2_out;  // OR_Gate or_2, 5 bits wide
  Comparator #(.width(5), .mode("unsigned")) comparator_2 (.a(or_2_out), .b(register_2_q), .eq(out_6));  // open: gt, lt
endmodule
