// Logisim project P3_L0_CPU_3.0.circ as structural Verilog: 13 circuits, main circuit main
module main (
  input  Reset,
  output [31:0] out_2,
  output out_3,
  output [4:0] out_4,
  output [31:0] out_5,
  output out_6,
  output [4:0] out_7,
  output [31:0] out_8
);

  wire alu_1_zero, and_1_out, Clk, Control_Unit_alusrc, Control_Unit_branch, Control_Unit_extop,
       Control_Unit_jump, Control_Unit_memtoreg, Control_Unit_regdst, Control_Unit_tohigh_16;
  wire [1:0] Control_Unit_dmop;
  wire [2:0] Control_Unit_alu_control;
  wire [27:0] bit_extender_1_out, shifter_1_out;
  wire [31:0] adder_1_out, adder_2_out, alu_1_alu_result, begin_1_out_2, begin_2_out_2, data_memory_1_rd,
       extend_1_out_3, multiplexer_1_out, multiplexer_2_out, multiplexer_3_out, multiplexer_5_out, or_1_out,
       or_2_out, pc_1_pc, registers_1_rd1, shifter_2_out;

  Clock u_Clk (.out(Clk));
  Multiplexer #(.width(32), .disabled(0), .enable("false")) multiplexer_1 (
    .in0(adder_1_out), .in1(adder_2_out), .out(multiplexer_1_out), .sel(and_1_out));
  Multiplexer #(.width(32), .disabled(0), .enable("false")) multiplexer_2 (
    .in0(multiplexer_1_out), .in1({adder_1_out[31:28], shifter_1_out}), .out(multiplexer_2_out),
    .sel(Control_Unit_jump));
  Begin begin_1 (.out_2(begin_1_out_2), .in_1(Clk));
  PC pc_1 (.PC_prime(or_1_out), .Clk(Clk), .Reset(Reset), .PC(pc_1_pc));
  assign or_1_out = multiplexer_2_out | begin_1_out_2;  // OR_Gate or_1, 32 bits wide
  Instruction_Memory instruction_memory_1 (.PC(pc_1_pc), .Instr(out_2));
  Adder #(.width(32)) adder_1 (.a(pc_1_pc), .b(32'h4), .out(adder_1_out));  // open: cin, cout
  Control_Unit Control_Unit (
    .Jump(Control_Unit_jump), .Op(out_2[31:26]), .Funct(out_2[5:0]), .MemtoReg(Control_Unit_memtoreg),
    .MemWrite(out_6), .Branch(Control_Unit_branch), .ALU_Control(Control_Unit_alu_control),
    .ALUSrc(Control_Unit_alusrc), .RegDst(Control_Unit_regdst), .RegWrite(out_3), .EXTop(Control_Unit_extop),
    .ToHigh_16(Control_Unit_tohigh_16), .DMop(Control_Unit_dmop));
  Registers registers_1 (
    .A1(out_2[25:21]), .A2(out_2[20:16]), .A3(out_4), .WD3(out_5), .RD1(registers_1_rd1), .RD2(out_8),
    .in_1(Clk), .in_2(out_3), .in_7(Reset));
  Extend extend_1 (.in_2(out_2[15:0]), .out_3(extend_1_out_3), .in_1(Control_Unit_extop));
  assign bit_extender_1_out = {{2{1'b0}}, out_2[25:0]};  // Bit_Extender bit_extender_1
  Multiplexer #(.width(32), .disabled(0), .enable("false")) multiplexer_3 (
    .in0(out_8), .in1(extend_1_out_3), .out(multiplexer_3_out), .sel(Control_Unit_alusrc));
  Multiplexer #(.width(5), .disabled(0), .enable("false")) multiplexer_4 (
    .in0(out_2[20:16]), .in1(out_2[15:11]), .out(out_4), .sel(Control_Unit_regdst));
  Shifter #(.width(28)) shifter_1 (.in(bit_extender_1_out), .\dist (5'b00010), .out(shifter_1_out));
  // Probe on Control_Unit_alu_control
  ALU alu_1 (
    .SrcA(registers_1_rd1), .SrcB(multiplexer_3_out), .ALU_Result(alu_1_alu_result),
    .ALU_Control(Control_Unit_alu_control), .Zero(alu_1_zero));
  Shifter #(.width(32)) shifter_2 (.in(extend_1_out_3), .\dist (5'b00010), .out(shifter_2_out));
  and and_1 (and_1_out, Control_Unit_branch, alu_1_zero);
  Multiplexer #(.width(32), .disabled(0), .enable("false")) multiplexer_5 (
    .in0(alu_1_alu_result), .in1({out_2[15:0], {16{1'b0}}}),
    .out({multiplexer_5_out[31:7], out_7, multiplexer_5_out[1:0]}), .sel(Control_Unit_tohigh_16));
  Begin begin_2 (.out_2(begin_2_out_2), .in_1(Clk));
  // Probe on {out_2[15:0], {16{1'b0}}}
  Adder #(.width(32)) adder_2 (.a(shifter_2_out), .b(adder_1_out), .out(adder_2_out));  // open: cin, cout
  assign or_2_out = {multiplexer_5_out[31:7], out_7, multiplexer_5_out[1:0]} | begin_2_out_2;  // OR_Gate or_2, 32 bits wide
  // Probe on Control_Unit_dmop
  Data_Memory data_memory_1 (
    .A(or_2_out), .WD(out_8), .RD(data_memory_1_rd), .in_1(Clk), .in_2(out_6), .in_6(Reset),
    .in_3(Control_Unit_dmop));
  // Probe on out_5
  Multiplexer #(.width(32), .disabled(0), .enable("false")) multiplexer_6 (
    .in0(or_2_out), .in1(data_memory_1_rd), .out(out_5), .sel(Control_Unit_memtoreg));
  // Probe on out_2
  // Probe on out_4

  // Other names for the same wires on the sheet: Instr[31:0] = out_2; MemAddr[4:0] = out_7; MemData[31:0] = out_8;
  //   MemWrite = out_6; RegAddr[4:0] = out_4; RegData[31:0] = out_5; RegWrite = out_3
endmodule

module PC (
  input  [31:0] PC_prime,
  input  Clk,
  input  Reset,
  output [31:0] PC
);

  Register #(.width(32)) u_PC (.D(PC_prime), .Q(PC), .clk(Clk), .clr(Reset));  // open: en
endmodule

// IM
module Instruction_Memory (
  input  [31:0] PC,
  output [31:0] Instr
);

  // Probe on PC[6:2]
  ROM #(.addrWidth(5), .dataWidth(32)) rom_1 (.addr(PC[6:2]), .data(Instr));  // open: sel

  // Notes on the sheet:
  //   contents of rom_1 (hex, n*v repeats v):
  //   341c0000 341d0000 340080f8 36ee0367 3593769c 34dda539 3465c5dc 34be0ff1 3472af1d 35566602 35fe72a7
  //   3437ff23 37b9649e 3690bf9b 37fe4e0c 3711f49d 3c113bfe 3c057433 3c03c451 3c04c431 3c1c24d9 3c1bf0da
  //   3c0ccc68 3c0a118d 3c1021ea 3c0004d3 3c16115b 3c184f06 3c1215de 1000ffff
endmodule

module in (
  input  in_1,
  input  [31:0] in_2,
  input  [4:0] in_3,
  output [31:0] out_4,
  output [31:0] out_5,
  output [31:0] out_6,
  output [31:0] out_7,
  output [31:0] out_8,
  output [31:0] out_9,
  output [31:0] out_10,
  output [31:0] out_11,
  output [31:0] out_12,
  output [31:0] out_13,
  output [31:0] out_14,
  output [31:0] out_15,
  output [31:0] out_16,
  output [31:0] out_17,
  output [31:0] out_18,
  output [31:0] out_19,
  output [31:0] out_20,
  output [31:0] out_21,
  output [31:0] out_22,
  output [31:0] out_23,
  output [31:0] out_24,
  output [31:0] out_25,
  output [31:0] out_26,
  output [31:0] out_27,
  output [31:0] out_28,
  output [31:0] out_29,
  output [31:0] out_30,
  output [31:0] out_31,
  output [31:0] out_32,
  output [31:0] out_33,
  output [31:0] out_34,
  output [31:0] out_35,
  output out_36,
  output out_37,
  output out_38,
  output out_39,
  output out_40,
  output out_41,
  output out_42,
  output out_43,
  output out_44,
  output out_45,
  output out_46,
  output out_47,
  output out_48,
  output out_49,
  output out_50,
  output out_51,
  output out_52,
  output out_53,
  output out_54,
  output out_55,
  output out_56,
  output out_57,
  output out_58,
  output out_59,
  output out_60,
  output out_61,
  output out_62,
  output out_63,
  output out_64,
  output out_65,
  output out_66,
  output out_67
);

  Demultiplexer #(.select(5), .width(32)) demultiplexer_1 (
    .out0(out_4), .out1(out_5), .out2(out_6), .out3(out_7), .out4(out_8), .out5(out_9), .out6(out_10),
    .out7(out_11), .out8(out_12), .out9(out_13), .out10(out_14), .out11(out_15), .out12(out_16),
    .out13(out_17), .out14(out_18), .out15(out_19), .out16(out_20), .out17(out_21), .out18(out_22),
    .out19(out_23), .out20(out_24), .out21(out_25), .out22(out_26), .out23(out_27), .out24(out_28),
    .out25(out_29), .out26(out_30), .out27(out_31), .out28(out_32), .out29(out_33), .out30(out_34),
    .out31(out_35), .in(in_2), .sel(in_3), .en(in_1));
  Decoder #(.select(5)) decoder_1 (
    .out0(out_36), .out1(out_37), .out2(out_38), .out3(out_39), .out4(out_40), .out5(out_41), .out6(out_42),
    .out7(out_43), .out8(out_44), .out9(out_45), .out10(out_46), .out11(out_47), .out12(out_48),
    .out13(out_49), .out14(out_50), .out15(out_51), .out16(out_52), .out17(out_53), .out18(out_54),
    .out19(out_55), .out20(out_56), .out21(out_57), .out22(out_58), .out23(out_59), .out24(out_60),
    .out25(out_61), .out26(out_62), .out27(out_63), .out28(out_64), .out29(out_65), .out30(out_66),
    .out31(out_67), .sel(in_3), .en(in_1));

  // Other names for the same wires on the sheet: en = in_1
endmodule

module _32_rigister (
  input  in_1,
  input  in_2,
  input  [31:0] _0,
  input  en1,
  input  [31:0] _1,
  input  en2,
  input  [31:0] _2,
  input  en3,
  input  [31:0] _3,
  input  en4,
  input  [31:0] _4,
  input  en1_2,
  input  [31:0] _5,
  input  en2_2,
  input  [31:0] _6,
  input  en3_2,
  input  [31:0] _7,
  input  en4_2,
  input  [31:0] _8,
  input  en1_3,
  input  [31:0] _9,
  input  en2_3,
  input  [31:0] _10,
  input  en3_3,
  input  [31:0] _11,
  input  en4_3,
  input  [31:0] _12,
  input  en1_4,
  input  [31:0] _13,
  input  en2_4,
  input  [31:0] _14,
  input  en3_4,
  input  [31:0] _15,
  input  en4_4,
  input  [31:0] _16,
  input  en1_5,
  input  [31:0] _17,
  input  en2_5,
  input  [31:0] _18,
  input  en3_5,
  input  [31:0] _19,
  input  en4_5,
  input  [31:0] _20,
  input  en1_6,
  input  [31:0] _21,
  input  en2_6,
  input  [31:0] _22,
  input  en3_6,
  input  [31:0] _23,
  input  en4_6,
  input  [31:0] _24,
  input  en1_7,
  input  [31:0] _25,
  input  en2_7,
  input  [31:0] _26,
  input  en3_7,
  input  [31:0] _27,
  input  en4_7,
  input  [31:0] _28,
  input  en1_8,
  input  [31:0] _29,
  input  en2_8,
  input  [31:0] _30,
  input  en3_8,
  input  [31:0] _31,
  input  en4_8,
  output [31:0] out_67,
  output [31:0] out_68,
  output [31:0] out_69,
  output [31:0] out_70,
  output [31:0] out_71,
  output [31:0] out_72,
  output [31:0] out_73,
  output [31:0] out_74,
  output [31:0] out_75,
  output [31:0] out_76,
  output [31:0] out_77,
  output [31:0] out_78,
  output [31:0] out_79,
  output [31:0] out_80,
  output [31:0] out_81,
  output [31:0] out_82,
  output [31:0] out_83,
  output [31:0] out_84,
  output [31:0] out_85,
  output [31:0] out_86,
  output [31:0] out_87,
  output [31:0] out_88,
  output [31:0] out_89,
  output [31:0] out_90,
  output [31:0] out_91,
  output [31:0] out_92,
  output [31:0] out_93,
  output [31:0] out_94,
  output [31:0] out_95,
  output [31:0] out_96,
  output [31:0] out_97,
  output [31:0] out_98
);

  Register #(.width(32)) register_1 (.D(_0), .en(1'b0), .Q(out_67), .clk(in_1), .clr(in_2));
  Register #(.width(32)) register_2 (.D(_1), .en(en2), .Q(out_68), .clk(in_1), .clr(in_2));
  Register #(.width(32)) register_3 (.D(_2), .en(en3), .Q(out_69), .clk(in_1), .clr(in_2));
  Register #(.width(32)) register_4 (.D(_3), .en(en4), .Q(out_70), .clk(in_1), .clr(in_2));
  Register #(.width(32)) register_5 (.D(_4), .en(en1_2), .Q(out_71), .clk(in_1), .clr(in_2));
  Register #(.width(32)) register_6 (.D(_5), .en(en2_2), .Q(out_72), .clk(in_1), .clr(in_2));
  Register #(.width(32)) register_7 (.D(_6), .en(en3_2), .Q(out_73), .clk(in_1), .clr(in_2));
  Register #(.width(32)) register_8 (.D(_7), .en(en4_2), .Q(out_74), .clk(in_1), .clr(in_2));
  Register #(.width(32)) register_9 (.D(_8), .en(en1_3), .Q(out_75), .clk(in_1), .clr(in_2));
  Register #(.width(32)) register_10 (.D(_9), .en(en2_3), .Q(out_76), .clk(in_1), .clr(in_2));
  Register #(.width(32)) register_11 (.D(_10), .en(en3_3), .Q(out_77), .clk(in_1), .clr(in_2));
  Register #(.width(32)) register_12 (.D(_11), .en(en4_3), .Q(out_78), .clk(in_1), .clr(in_2));
  Register #(.width(32)) register_13 (.D(_12), .en(en1_4), .Q(out_79), .clk(in_1), .clr(in_2));
  Register #(.width(32)) register_14 (.D(_13), .en(en2_4), .Q(out_80), .clk(in_1), .clr(in_2));
  Register #(.width(32)) register_15 (.D(_14), .en(en3_4), .Q(out_81), .clk(in_1), .clr(in_2));
  Register #(.width(32)) register_16 (.D(_15), .en(en4_4), .Q(out_82), .clk(in_1), .clr(in_2));
  Register #(.width(32)) register_17 (.D(_16), .en(en1_5), .Q(out_83), .clk(in_1), .clr(in_2));
  Register #(.width(32)) register_18 (.D(_17), .en(en2_5), .Q(out_84), .clk(in_1), .clr(in_2));
  Register #(.width(32)) register_19 (.D(_18), .en(en3_5), .Q(out_85), .clk(in_1), .clr(in_2));
  Register #(.width(32)) register_20 (.D(_19), .en(en4_5), .Q(out_86), .clk(in_1), .clr(in_2));
  Register #(.width(32)) register_21 (.D(_20), .en(en1_6), .Q(out_87), .clk(in_1), .clr(in_2));
  Register #(.width(32)) register_22 (.D(_21), .en(en2_6), .Q(out_88), .clk(in_1), .clr(in_2));
  Register #(.width(32)) register_23 (.D(_22), .en(en3_6), .Q(out_89), .clk(in_1), .clr(in_2));
  Register #(.width(32)) register_24 (.D(_23), .en(en4_6), .Q(out_90), .clk(in_1), .clr(in_2));
  Register #(.width(32)) register_25 (.D(_24), .en(en1_7), .Q(out_91), .clk(in_1), .clr(in_2));
  Register #(.width(32)) register_26 (.D(_25), .en(en2_7), .Q(out_92), .clk(in_1), .clr(in_2));
  Register #(.width(32)) register_27 (.D(_26), .en(en3_7), .Q(out_93), .clk(in_1), .clr(in_2));
  Register #(.width(32)) register_28 (.D(_27), .en(en4_7), .Q(out_94), .clk(in_1), .clr(in_2));
  Register #(.width(32)) register_29 (.D(_28), .en(en1_8), .Q(out_95), .clk(in_1), .clr(in_2));
  Register #(.width(32)) register_30 (.D(_29), .en(en2_8), .Q(out_96), .clk(in_1), .clr(in_2));
  Register #(.width(32)) register_31 (.D(_30), .en(en3_8), .Q(out_97), .clk(in_1), .clr(in_2));
  Register #(.width(32)) register_32 (.D(_31), .en(en4_8), .Q(out_98), .clk(in_1), .clr(in_2));

  // Other names for the same wires on the sheet: clk = in_1; reset = in_2
endmodule

// GRF
module Registers (
  input  in_1,
  input  in_2,
  input  [4:0] A1,
  input  [4:0] A2,
  input  [4:0] A3,
  input  [31:0] WD3,
  input  in_7,
  output [31:0] RD1,
  output [31:0] RD2
);

  wire in_1_out_36, in_1_out_37, in_1_out_38, in_1_out_39, in_1_out_40, in_1_out_41, in_1_out_42,
       in_1_out_43, in_1_out_44, in_1_out_45, in_1_out_46, in_1_out_47, in_1_out_48, in_1_out_49,
       in_1_out_50, in_1_out_51, in_1_out_52, in_1_out_53, in_1_out_54, in_1_out_55, in_1_out_56,
       in_1_out_57, in_1_out_58, in_1_out_59, in_1_out_60, in_1_out_61, in_1_out_62, in_1_out_63,
       in_1_out_64, in_1_out_65, in_1_out_66, in_1_out_67;
  wire [31:0] in_1_out_4, in_1_out_5, in_1_out_6, in_1_out_7, in_1_out_8, in_1_out_9, in_1_out_10,
       in_1_out_11, in_1_out_12, in_1_out_13, in_1_out_14, in_1_out_15, in_1_out_16, in_1_out_17,
       in_1_out_18, in_1_out_19, in_1_out_20, in_1_out_21, in_1_out_22, in_1_out_23, in_1_out_24,
       in_1_out_25, in_1_out_26, in_1_out_27, in_1_out_28, in_1_out_29, in_1_out_30, in_1_out_31,
       in_1_out_32, in_1_out_33, in_1_out_34, in_1_out_35, n32_rigister_1_out_67, n32_rigister_1_out_68,
       n32_rigister_1_out_69, n32_rigister_1_out_70, n32_rigister_1_out_71, n32_rigister_1_out_72,
       n32_rigister_1_out_73, n32_rigister_1_out_74, n32_rigister_1_out_75, n32_rigister_1_out_76,
       n32_rigister_1_out_77, n32_rigister_1_out_78, n32_rigister_1_out_79, n32_rigister_1_out_80,
       n32_rigister_1_out_81, n32_rigister_1_out_82, n32_rigister_1_out_83, n32_rigister_1_out_84,
       n32_rigister_1_out_85, n32_rigister_1_out_86, n32_rigister_1_out_87, n32_rigister_1_out_88,
       n32_rigister_1_out_89, n32_rigister_1_out_90, n32_rigister_1_out_91, n32_rigister_1_out_92,
       n32_rigister_1_out_93, n32_rigister_1_out_94, n32_rigister_1_out_95, n32_rigister_1_out_96,
       n32_rigister_1_out_97, n32_rigister_1_out_98;

  in u_in_1 (
    .in_2(WD3), .in_3(A3), .in_1(in_2), .out_4(in_1_out_4), .out_5(in_1_out_5), .out_6(in_1_out_6),
    .out_7(in_1_out_7), .out_8(in_1_out_8), .out_9(in_1_out_9), .out_10(in_1_out_10), .out_11(in_1_out_11),
    .out_12(in_1_out_12), .out_13(in_1_out_13), .out_14(in_1_out_14), .out_15(in_1_out_15),
    .out_16(in_1_out_16), .out_17(in_1_out_17), .out_18(in_1_out_18), .out_19(in_1_out_19),
    .out_20(in_1_out_20), .out_21(in_1_out_21), .out_22(in_1_out_22), .out_23(in_1_out_23),
    .out_24(in_1_out_24), .out_25(in_1_out_25), .out_26(in_1_out_26), .out_27(in_1_out_27),
    .out_28(in_1_out_28), .out_29(in_1_out_29), .out_30(in_1_out_30), .out_31(in_1_out_31),
    .out_32(in_1_out_32), .out_33(in_1_out_33), .out_34(in_1_out_34), .out_35(in_1_out_35),
    .out_36(in_1_out_36), .out_37(in_1_out_37), .out_38(in_1_out_38), .out_39(in_1_out_39),
    .out_40(in_1_out_40), .out_41(in_1_out_41), .out_42(in_1_out_42), .out_43(in_1_out_43),
    .out_44(in_1_out_44), .out_45(in_1_out_45), .out_46(in_1_out_46), .out_47(in_1_out_47),
    .out_48(in_1_out_48), .out_49(in_1_out_49), .out_50(in_1_out_50), .out_51(in_1_out_51),
    .out_52(in_1_out_52), .out_53(in_1_out_53), .out_54(in_1_out_54), .out_55(in_1_out_55),
    .out_56(in_1_out_56), .out_57(in_1_out_57), .out_58(in_1_out_58), .out_59(in_1_out_59),
    .out_60(in_1_out_60), .out_61(in_1_out_61), .out_62(in_1_out_62), .out_63(in_1_out_63),
    .out_64(in_1_out_64), .out_65(in_1_out_65), .out_66(in_1_out_66), .out_67(in_1_out_67));
  _32_rigister u_32_rigister_1 (
    ._0(in_1_out_4), ._1(in_1_out_5), ._2(in_1_out_6), ._3(in_1_out_7), ._4(in_1_out_8), ._5(in_1_out_9),
    ._6(in_1_out_10), ._7(in_1_out_11), ._8(in_1_out_12), ._9(in_1_out_13), ._10(in_1_out_14),
    ._11(in_1_out_15), ._12(in_1_out_16), ._13(in_1_out_17), ._14(in_1_out_18), ._15(in_1_out_19),
    ._16(in_1_out_20), ._17(in_1_out_21), ._18(in_1_out_22), ._19(in_1_out_23), ._20(in_1_out_24),
    ._21(in_1_out_25), ._22(in_1_out_26), ._23(in_1_out_27), ._24(in_1_out_28), ._25(in_1_out_29),
    ._26(in_1_out_30), ._27(in_1_out_31), ._28(in_1_out_32), ._29(in_1_out_33), ._30(in_1_out_34),
    ._31(in_1_out_35), .in_1(in_1), .in_2(in_7), .en1(in_1_out_36), .en2(in_1_out_37), .en3(in_1_out_38),
    .en4(in_1_out_39), .en1_2(in_1_out_40), .en2_2(in_1_out_41), .en3_2(in_1_out_42), .en4_2(in_1_out_43),
    .en1_3(in_1_out_44), .en2_3(in_1_out_45), .en3_3(in_1_out_46), .en4_3(in_1_out_47), .en1_4(in_1_out_48),
    .en2_4(in_1_out_49), .en3_4(in_1_out_50), .en4_4(in_1_out_51), .en1_5(in_1_out_52), .en2_5(in_1_out_53),
    .en3_5(in_1_out_54), .en4_5(in_1_out_55), .en1_6(in_1_out_56), .en2_6(in_1_out_57), .en3_6(in_1_out_58),
    .en4_6(in_1_out_59), .en1_7(in_1_out_60), .en2_7(in_1_out_61), .en3_7(in_1_out_62), .en4_7(in_1_out_63),
    .en1_8(in_1_out_64), .en2_8(in_1_out_65), .en3_8(in_1_out_66), .en4_8(in_1_out_67),
    .out_67(n32_rigister_1_out_67), .out_68(n32_rigister_1_out_68), .out_69(n32_rigister_1_out_69),
    .out_70(n32_rigister_1_out_70), .out_71(n32_rigister_1_out_71), .out_72(n32_rigister_1_out_72),
    .out_73(n32_rigister_1_out_73), .out_74(n32_rigister_1_out_74), .out_75(n32_rigister_1_out_75),
    .out_76(n32_rigister_1_out_76), .out_77(n32_rigister_1_out_77), .out_78(n32_rigister_1_out_78),
    .out_79(n32_rigister_1_out_79), .out_80(n32_rigister_1_out_80), .out_81(n32_rigister_1_out_81),
    .out_82(n32_rigister_1_out_82), .out_83(n32_rigister_1_out_83), .out_84(n32_rigister_1_out_84),
    .out_85(n32_rigister_1_out_85), .out_86(n32_rigister_1_out_86), .out_87(n32_rigister_1_out_87),
    .out_88(n32_rigister_1_out_88), .out_89(n32_rigister_1_out_89), .out_90(n32_rigister_1_out_90),
    .out_91(n32_rigister_1_out_91), .out_92(n32_rigister_1_out_92), .out_93(n32_rigister_1_out_93),
    .out_94(n32_rigister_1_out_94), .out_95(n32_rigister_1_out_95), .out_96(n32_rigister_1_out_96),
    .out_97(n32_rigister_1_out_97), .out_98(n32_rigister_1_out_98));
  Multiplexer #(.select(5), .width(32), .enable("false")) multiplexer_1 (
    .in0(n32_rigister_1_out_67), .in1(n32_rigister_1_out_68), .in2(n32_rigister_1_out_69),
    .in3(n32_rigister_1_out_70), .in4(n32_rigister_1_out_71), .in5(n32_rigister_1_out_72),
    .in6(n32_rigister_1_out_73), .in7(n32_rigister_1_out_74), .in8(n32_rigister_1_out_75),
    .in9(n32_rigister_1_out_76), .in10(n32_rigister_1_out_77), .in11(n32_rigister_1_out_78),
    .in12(n32_rigister_1_out_79), .in13(n32_rigister_1_out_80), .in14(n32_rigister_1_out_81),
    .in15(n32_rigister_1_out_82), .in16(n32_rigister_1_out_83), .in17(n32_rigister_1_out_84),
    .in18(n32_rigister_1_out_85), .in19(n32_rigister_1_out_86), .in20(n32_rigister_1_out_87),
    .in21(n32_rigister_1_out_88), .in22(n32_rigister_1_out_89), .in23(n32_rigister_1_out_90),
    .in24(n32_rigister_1_out_91), .in25(n32_rigister_1_out_92), .in26(n32_rigister_1_out_93),
    .in27(n32_rigister_1_out_94), .in28(n32_rigister_1_out_95), .in29(n32_rigister_1_out_96),
    .in30(n32_rigister_1_out_97), .in31(n32_rigister_1_out_98), .out(RD1), .sel(A1));
  Multiplexer #(.select(5), .width(32), .enable("false")) multiplexer_2 (
    .in0(n32_rigister_1_out_67), .in1(n32_rigister_1_out_68), .in2(n32_rigister_1_out_69),
    .in3(n32_rigister_1_out_70), .in4(n32_rigister_1_out_71), .in5(n32_rigister_1_out_72),
    .in6(n32_rigister_1_out_73), .in7(n32_rigister_1_out_74), .in8(n32_rigister_1_out_75),
    .in9(n32_rigister_1_out_76), .in10(n32_rigister_1_out_77), .in11(n32_rigister_1_out_78),
    .in12(n32_rigister_1_out_79), .in13(n32_rigister_1_out_80), .in14(n32_rigister_1_out_81),
    .in15(n32_rigister_1_out_82), .in16(n32_rigister_1_out_83), .in17(n32_rigister_1_out_84),
    .in18(n32_rigister_1_out_85), .in19(n32_rigister_1_out_86), .in20(n32_rigister_1_out_87),
    .in21(n32_rigister_1_out_88), .in22(n32_rigister_1_out_89), .in23(n32_rigister_1_out_90),
    .in24(n32_rigister_1_out_91), .in25(n32_rigister_1_out_92), .in26(n32_rigister_1_out_93),
    .in27(n32_rigister_1_out_94), .in28(n32_rigister_1_out_95), .in29(n32_rigister_1_out_96),
    .in30(n32_rigister_1_out_97), .in31(n32_rigister_1_out_98), .out(RD2), .sel(A2));

  // Other names for the same wires on the sheet: clk = in_1; en = in_2; reset = in_7
endmodule

// DM
module Data_Memory (
  input  in_1,
  input  in_2,
  input  [1:0] in_3,
  input  [31:0] A,
  input  [31:0] WD,
  input  in_6,
  output [31:0] RD
);

  wire decoder_1_out0, decoder_1_out1, decoder_1_out2, decoder_1_out3, decoder_2_out0, decoder_2_out1;
  wire [7:0] multiplexer_8_out, R_0_7, R_16_23;
  wire [15:0] multiplexer_9_out;
  wire [15:8] R_0_15, R_16_31;
  wire [31:0] ReadB, ReadH, WriteB, WriteData, WriteH;

  Decoder #(.select(2), .disabled(0), .enable("false")) decoder_1 (
    .out0(decoder_1_out0), .out1(decoder_1_out1), .out2(decoder_1_out2), .out3(decoder_1_out3), .sel(A[1:0]));
  Decoder #(.disabled(0), .enable("false")) decoder_2 (.out0(decoder_2_out0), .out1(decoder_2_out1), .sel(A[1]));
  Multiplexer #(.select(2), .width(32), .disabled(0), .enable("false")) multiplexer_1 (
    .in0(WD), .in1(WriteB), .in2(WriteH), .out(WriteData), .sel(in_3));  // open: in3
  Multiplexer #(.width(8), .disabled(0), .enable("false")) multiplexer_2 (
    .in0(R_0_7), .in1(WD[7:0]), .out(WriteB[7:0]), .sel(decoder_1_out0));
  Multiplexer #(.width(8), .disabled(0), .enable("false")) multiplexer_3 (
    .in0(R_0_15), .in1(WD[7:0]), .out(WriteB[15:8]), .sel(decoder_1_out1));
  Multiplexer #(.width(8), .disabled(0), .enable("false")) multiplexer_4 (
    .in0(R_16_23), .in1(WD[7:0]), .out(WriteB[23:16]), .sel(decoder_1_out2));
  Multiplexer #(.width(8), .disabled(0), .enable("false")) multiplexer_5 (
    .in0(R_16_31), .in1(WD[7:0]), .out(WriteB[31:24]), .sel(decoder_1_out3));
  Multiplexer #(.width(16), .disabled(0), .enable("false")) multiplexer_6 (
    .in0({R_0_15, R_0_7}), .in1(WD[15:0]), .out(WriteH[15:0]), .sel(decoder_2_out0));
  Multiplexer #(.width(16), .disabled(0), .enable("false")) multiplexer_7 (
    .in0({R_16_31, R_16_23}), .in1(WD[15:0]), .out(WriteH[31:16]), .sel(decoder_2_out1));
  RAM #(.addrWidth(5), .dataWidth(32), .bus("separate")) ram_1 (
    .addr(A[6:2]), .din(WriteData), .data({R_16_31, R_16_23, R_0_15, R_0_7}), .str(in_2), .clk(in_1),
    .clr(in_6));  // open: sel, ld
  Multiplexer #(.select(2), .width(8), .disabled(0), .enable("false")) multiplexer_8 (
    .in0(R_0_7), .in1(R_0_15), .in2(R_16_23), .in3(R_16_31), .out(multiplexer_8_out), .sel(A[1:0]));
  Multiplexer #(.width(16), .enable("false")) multiplexer_9 (
    .in0({R_0_15, R_0_7}), .in1({R_16_31, R_16_23}), .out(multiplexer_9_out), .sel(A[1]));
  assign ReadB = {{24{1'b0}}, multiplexer_8_out};  // Bit_Extender bit_extender_1
  assign ReadH = {{16{1'b0}}, multiplexer_9_out};  // Bit_Extender bit_extender_2
  Multiplexer #(.select(2), .width(32), .disabled(0), .enable("false")) multiplexer_10 (
    .in0({R_16_31, R_16_23, R_0_15, R_0_7}), .in1(ReadB), .in2(ReadH), .out(RD), .sel(in_3));  // open: in3

  // Other names for the same wires on the sheet: Byte[1:0] = A[1:0]; Half = A[1]; Address[4:0] = A[6:2]; Clk = in_1;
  //   DMop[1:0] = in_3; R_0_15[7:0] = R_0_7; ReadW[31:0] = {R_16_31, R_16_23, R_0_15, R_0_7}; R_8_15[7:0] = R_0_15;
  //   R_16_31[7:0] = R_16_23; R_24_31[7:0] = R_16_31; ReadData[31:0] = RD; Reset = in_6; W_0_7[7:0] = WD[7:0];
  //   W_0_15[15:0] = WD[15:0]; WriteW[31:0] = WD; W_8_15[7:0] = WD[15:8]; W_16_23[7:0] = WD[23:16];
  //   W_16_31[15:0] = WD[31:16]; W_24_31[7:0] = WD[31:24]; We = in_2
endmodule

module Control_Unit (
  input  [5:0] Op,
  input  [5:0] Funct,
  output Jump,
  output MemtoReg,
  output [1:0] DMop,
  output MemWrite,
  output Branch,
  output [2:0] ALU_Control,
  output ALUSrc,
  output RegDst,
  output ToHigh_16,
  output EXTop,
  output RegWrite
);

  wire ALUop_0, ALUop_1, ALUop_2, Get_Instruction_addi, Get_Instruction_beq, Get_Instruction_j,
       Get_Instruction_lb, Get_Instruction_lh, Get_Instruction_lui, Get_Instruction_lw, Get_Instruction_ori,
       Get_Instruction_out_14, Get_Instruction_out_15, Get_Instruction_out_16, Get_Instruction_r,
       Get_Instruction_sb, Get_Instruction_sh, Get_Instruction_sw, Get_R_Instruction__r,
       Get_R_Instruction_add, Get_R_Instruction_addu, Get_R_Instruction_and, Get_R_Instruction_beq,
       Get_R_Instruction_or, Get_R_Instruction_ori, Get_R_Instruction_out_20, Get_R_Instruction_out_21,
       Get_R_Instruction_out_22, Get_R_Instruction_out_23, Get_R_Instruction_out_24,
       Get_R_Instruction_out_25, Get_R_Instruction_slt, Get_R_Instruction_sub, Get_R_Instruction_subu;

  Get_Instruction Get_Instruction (
    .Op(Op), .R(Get_Instruction_r), .lw(Get_Instruction_lw), .sw(Get_Instruction_sw),
    .beq(Get_Instruction_beq), .addi(Get_Instruction_addi), .j(Get_Instruction_j), .ori(Get_Instruction_ori),
    .lui(Get_Instruction_lui), .lb(Get_Instruction_lb), .sb(Get_Instruction_sb), .lh(Get_Instruction_lh),
    .sh(Get_Instruction_sh), .out_14(Get_Instruction_out_14), .out_15(Get_Instruction_out_15),
    .out_16(Get_Instruction_out_16));
  or or_1 (RegWrite, Get_Instruction_r, Get_Instruction_lw, Get_Instruction_addi, Get_Instruction_ori, Get_Instruction_lui, Get_Instruction_lb, Get_Instruction_lh);
  Get_R_Instruction Get_R_Instruction (
    .ALUop_1(ALUop_1), .ALUop_0(ALUop_0), .Funct_5(Funct[5]), .Funct_4(Funct[4]), .Funct_3(Funct[3]),
    .Funct_2(Funct[2]), .Funct_1(Funct[1]), .Funct_0(Funct[0]), .beq(Get_R_Instruction_beq),
    .sub(Get_R_Instruction_sub), .slt(Get_R_Instruction_slt), ._R(Get_R_Instruction__r),
    .add(Get_R_Instruction_add), .\and (Get_R_Instruction_and), .\or (Get_R_Instruction_or),
    .ori(Get_R_Instruction_ori), .out_20(Get_R_Instruction_out_20), .out_21(Get_R_Instruction_out_21),
    .out_22(Get_R_Instruction_out_22), .out_23(Get_R_Instruction_out_23), .out_24(Get_R_Instruction_out_24),
    .addu(Get_R_Instruction_addu), .subu(Get_R_Instruction_subu), .ALUop_2(ALUop_2),
    .out_25(Get_R_Instruction_out_25));
  or or_2 (ALU_Control[2], Get_R_Instruction_beq, Get_R_Instruction_sub, Get_R_Instruction_slt, Get_R_Instruction_subu);
  or or_3 (EXTop, Get_Instruction_lw, Get_Instruction_sw, Get_Instruction_beq, Get_Instruction_addi, Get_Instruction_lb, Get_Instruction_sb, Get_Instruction_lh, Get_Instruction_sh);
  or or_4 (ALU_Control[1], Get_R_Instruction_beq, Get_R_Instruction__r, Get_R_Instruction_sub, Get_R_Instruction_slt, Get_R_Instruction_add, Get_R_Instruction_addu, Get_R_Instruction_subu);
  buf or_5 (RegDst, Get_Instruction_r);  // OR_Gate
  or or_6 (ALU_Control[0], Get_R_Instruction_slt, Get_R_Instruction_or, Get_R_Instruction_ori);
  or or_7 (ALUSrc, Get_Instruction_lw, Get_Instruction_sw, Get_Instruction_addi, Get_Instruction_ori, Get_Instruction_lui, Get_Instruction_lb, Get_Instruction_sb, Get_Instruction_lh, Get_Instruction_sh);
  buf or_8 (Branch, Get_Instruction_beq);  // OR_Gate
  or or_9 (MemWrite, Get_Instruction_sw, Get_Instruction_sb, Get_Instruction_sh);
  or or_10 (MemtoReg, Get_Instruction_lw, Get_Instruction_lb, Get_Instruction_lh);
  buf or_11 (Jump, Get_Instruction_j);  // OR_Gate
  buf or_12 (ALUop_2, 1'b0);  // OR_Gate
  or or_13 (ALUop_1, Get_Instruction_r, Get_Instruction_ori);
  or or_14 (ALUop_0, Get_Instruction_beq, Get_Instruction_ori);
  buf or_15 (ToHigh_16, Get_Instruction_lui);  // OR_Gate
  or or_16 (DMop[1], Get_Instruction_lh, Get_Instruction_sh);
  or or_17 (DMop[0], Get_Instruction_lb, Get_Instruction_sb);

  // Other names for the same wires on the sheet: ALU_Control_0 = ALU_Control[0]; ALU_Control_1 = ALU_Control[1];
  //   ALU_Control_2 = ALU_Control[2]; DMop_0 = DMop[0]; DMop_1 = DMop[1]
endmodule

module Get_Instruction (
  input  [5:0] Op,
  output R,
  output lw,
  output sw,
  output beq,
  output addi,
  output j,
  output ori,
  output lui,
  output lb,
  output sb,
  output lh,
  output sh,
  output out_14,
  output out_15,
  output out_16
);

  wire not_1_out, not_2_out, not_3_out, not_4_out, not_5_out, not_6_out;

  not not_1 (not_1_out, Op[5]);
  not not_2 (not_2_out, Op[3]);
  not not_3 (not_3_out, Op[4]);
  not not_4 (not_4_out, Op[1]);
  not not_5 (not_5_out, Op[2]);
  not not_6 (not_6_out, Op[0]);
  and u_R (R, not_1_out, not_3_out, not_2_out, not_5_out, not_4_out, not_6_out);
  and u_lw (lw, Op[5], not_3_out, not_2_out, not_5_out, Op[1], Op[0]);
  and u_sw (sw, Op[5], not_3_out, Op[3], not_5_out, Op[1], Op[0]);
  and u_beq (beq, not_1_out, not_3_out, not_2_out, Op[2], not_4_out, not_6_out);
  and u_addi (addi, not_1_out, not_3_out, Op[3], not_5_out, not_4_out, not_6_out);
  and u_j (j, not_1_out, not_3_out, not_2_out, not_5_out, Op[1], not_6_out);
  and u_ori (ori, not_1_out, not_3_out, Op[3], Op[2], not_4_out, Op[0]);
  and u_lui (lui, not_1_out, not_3_out, Op[3], Op[2], Op[1], Op[0]);
  and u_lb (lb, Op[5], not_3_out, not_2_out, not_5_out, not_4_out, not_6_out);
  and u_sb (sb, Op[5], not_3_out, Op[3], not_5_out, not_4_out, not_6_out);
  and u_lh (lh, Op[5], not_3_out, not_2_out, not_5_out, not_4_out, Op[0]);
  and u_sh (sh, Op[5], not_3_out, Op[3], not_5_out, not_4_out, Op[0]);
  // AND_Gate and_1 has open pins: out=out_14
  // AND_Gate and_2 has open pins: out=out_15
  // AND_Gate and_3 has open pins: out=out_16
endmodule

module Get_R_Instruction (
  input  ALUop_2,
  input  ALUop_1,
  input  ALUop_0,
  input  Funct_5,
  input  Funct_4,
  input  Funct_3,
  input  Funct_2,
  input  Funct_1,
  input  Funct_0,
  output beq,
  output sub,
  output slt,
  output _R,
  output add,
  output \and ,
  output \or ,
  output addu,
  output subu,
  output ori,
  output out_20,
  output out_21,
  output out_22,
  output out_23,
  output out_24,
  output out_25
);

  wire not_1_out, not_2_out, not_3_out, not_4_out, not_5_out, not_6_out, not_7_out, not_8_out, not_9_out;

  not not_1 (not_1_out, ALUop_2);
  not not_2 (not_2_out, ALUop_1);
  not not_3 (not_3_out, ALUop_0);
  not not_4 (not_4_out, Funct_5);
  not not_5 (not_5_out, Funct_4);
  not not_6 (not_6_out, Funct_3);
  not not_7 (not_7_out, Funct_2);
  not not_8 (not_8_out, Funct_1);
  not not_9 (not_9_out, Funct_0);
  and and_1 (sub, not_3_out, ALUop_1, Funct_5, not_5_out, not_6_out, not_7_out, Funct_1, not_9_out, not_1_out);
  and and_2 (slt, not_3_out, ALUop_1, Funct_5, not_5_out, Funct_3, not_7_out, Funct_1, not_9_out, not_1_out);
  and and_3 (add, not_3_out, ALUop_1, Funct_5, not_5_out, not_6_out, not_7_out, not_8_out, not_9_out, not_1_out);
  and and_4 (\and , not_3_out, ALUop_1, Funct_5, not_5_out, not_6_out, Funct_2, not_8_out, not_9_out, not_1_out);
  and and_5 (\or , not_3_out, ALUop_1, Funct_5, not_5_out, not_6_out, Funct_2, not_8_out, Funct_0, not_1_out);
  and and_6 (addu, not_3_out, ALUop_1, Funct_5, not_5_out, not_6_out, not_7_out, not_8_out, Funct_0, not_1_out);
  and and_7 (subu, not_3_out, ALUop_1, Funct_5, not_5_out, not_6_out, not_7_out, Funct_1, Funct_0, not_1_out);
  and and_8 (beq, not_2_out, not_1_out, ALUop_0);
  and and_9 (_R, not_2_out, not_1_out, not_3_out);
  and and_10 (ori, ALUop_1, not_1_out, ALUop_0);
endmodule

module ALU (
  input  [2:0] ALU_Control,
  input  [31:0] SrcA,
  input  [31:0] SrcB,
  output Zero,
  output [31:0] ALU_Result
);

  wire comparator_1_lt;
  wire [31:0] AND, AND__B, not_1_out, not_2_out, OR, OR__B, SLT, tunnel, tunnel_t, undriven;

  assign AND = SrcA & SrcB;  // AND_Gate and_1, 32 bits wide
  assign OR = SrcA | SrcB;  // OR_Gate or_1, 32 bits wide
  Comparator #(.width(32), .mode("unsigned")) comparator_1 (.a(SrcA), .b(SrcB), .lt(comparator_1_lt));  // open: gt, eq
  Adder #(.width(32)) adder_1 (.a(SrcA), .b(SrcB), .out(tunnel));  // open: cin, cout
  Subtractor #(.width(32)) subtractor_1 (.a(SrcA), .b(SrcB), .out(tunnel_t));  // open: bin, bout
  Multiplexer #(.select(3), .width(32), .disabled(0), .enable("false")) multiplexer_1 (
    .in0(AND), .in1(OR), .in2(tunnel), .in3(undriven), .in4(AND__B), .in5(OR__B), .in6(tunnel_t), .in7(SLT),
    .out(ALU_Result), .sel(ALU_Control));
  assign SLT = {{31{1'b0}}, comparator_1_lt};  // Bit_Extender bit_extender_1
  assign AND__B = SrcA & not_1_out;  // AND_Gate and_2, 32 bits wide
  assign not_1_out = ~SrcB;  // NOT_Gate not_1, 32 bits wide
  assign OR__B = SrcA | not_2_out;  // OR_Gate or_2, 32 bits wide
  assign not_2_out = ~SrcB;  // NOT_Gate not_2, 32 bits wide
  Comparator #(.width(32)) comparator_2 (.a({32{1'b0}}), .b(ALU_Result), .eq(Zero));  // open: gt, lt
endmodule

// EXT
module Extend (
  input  in_1,
  input  [15:0] in_2,
  output [31:0] out_3
);

  wire [31:0] bit_extender_1_out, bit_extender_2_out;

  assign bit_extender_1_out = {{16{1'b0}}, in_2};  // Bit_Extender bit_extender_1
  assign bit_extender_2_out = {{16{in_2[15]}}, in_2};  // Bit_Extender bit_extender_2
  Multiplexer #(.width(32), .disabled(0), .enable("false")) multiplexer_1 (
    .in0(bit_extender_1_out), .in1(bit_extender_2_out), .out(out_3), .sel(in_1));
endmodule

module Begin (
  input  in_1,
  output [31:0] out_2
);

  wire counter_1_q;

  Multiplexer #(.width(32), .disabled(0), .enable("false")) multiplexer_1 (
    .in0({32{1'b0}}), .in1({32{1'b0}}), .out(out_2), .sel(counter_1_q));
  Counter #(.width(1), .max('h1), .ongoal("stay")) counter_1 (
    .Q(counter_1_q), .clk(in_1));  // open: load, D, count, carry, clr

  // Other names for the same wires on the sheet: Begin[31:0] = out_2; clk = in_1
endmodule
