// Logisim project Logisim_fibonacci.circ as structural Verilog: 5 circuits, main circuit main
module main (
  input  [2:0] in_1,
  output [3:0] out_2
);

  wire and_1_out, clock_1_out, not_1_out;
  wire [2:0] n1_1_out_2, register_2_q, xnor_1_out;
  wire [3:0] add_1_out_3, register_1_q, register_3_q;

  // Probe on register_1_q
  Add add_1 (.in_1(register_1_q), .in_2(out_2), .out_3(add_1_out_3));
  _1 u_1_1 (.in_1(register_2_q), .out_2(n1_1_out_2));
  Clock clock_1 (.out(clock_1_out));
  // Probe on out_2
  Begin x__0_1_x (.in_1(register_3_q), .out_2(out_2));
  Register #(.width(4)) register_1 (.D(add_1_out_3), .en(not_1_out), .Q(register_1_q), .clk(clock_1_out));  // open: clr
  // Probe on register_2_q
  Register #(.width(3)) register_2 (.D(n1_1_out_2), .en(not_1_out), .Q(register_2_q), .clk(clock_1_out));  // open: clr
  not not_1 (not_1_out, and_1_out);
  // Probe on register_3_q
  Register #(.width(4)) register_3 (
    .D(register_1_q), .en(not_1_out), .Q(register_3_q), .clk(clock_1_out));  // open: clr
  and and_1 (and_1_out, xnor_1_out[0], xnor_1_out[1], xnor_1_out[2]);
  assign xnor_1_out = ~(register_2_q ^ in_1);  // XNOR_Gate xnor_1, 3 bits wide
  // Probe on xnor_1_out
  // Probe on and_1_out
endmodule

// (+1)
module _1 (
  input  [2:0] in_1,
  output [2:0] out_2
);

  wire and_1_out, and_2_out, and_3_out, and_4_out, and_5_out, not_1_out, not_2_out, not_3_out, not_4_out;

  not not_1 (not_1_out, in_1[0]);
  not not_2 (not_2_out, in_1[1]);
  not not_3 (not_3_out, in_1[2]);
  not not_4 (not_4_out, in_1[0]);
  xor xor_1 (out_2[0], 1'b1, in_1[0]);
  and and_1 (and_1_out, not_1_out, in_1[1]);
  and and_2 (and_2_out, in_1[0], not_2_out);
  and and_3 (and_3_out, not_2_out, in_1[2]);
  and and_4 (and_4_out, in_1[0], in_1[1], not_3_out);
  and and_5 (and_5_out, not_4_out, in_1[1], in_1[2]);
  or or_1 (out_2[1], and_1_out, and_2_out);
  or or_2 (out_2[2], and_3_out, and_4_out, and_5_out);
endmodule

module Add (
  input  [3:0] in_1,
  input  [3:0] in_2,
  output [3:0] out_3
);

  wire add_1_out_5, add_2_out_5, add_3_out_5;

  Add_2 add_1 (.in_1(in_1[0]), .in_2(in_2[0]), .in_3(1'b0), .out_4(out_3[0]), .out_5(add_1_out_5));
  Add_2 add_2 (.in_1(in_1[1]), .in_2(in_2[1]), .in_3(add_1_out_5), .out_4(out_3[1]), .out_5(add_2_out_5));
  Add_2 add_3 (.in_1(in_1[2]), .in_2(in_2[2]), .in_3(add_2_out_5), .out_4(out_3[2]), .out_5(add_3_out_5));
  Add_2 add_4 (.in_1(in_1[3]), .in_2(in_2[3]), .in_3(add_3_out_5), .out_4(out_3[3]));  // open: out_5
endmodule

module Begin (
  input  [3:0] in_1,
  output [3:0] out_2
);

  wire nor_1_out;

  nor nor_1 (nor_1_out, in_1[0], in_1[1], in_1[2], in_1[3]);
  or or_1 (out_2[0], nor_1_out, in_1[0]);

  assign out_2[3:1] = in_1[3:1];
endmodule

module Add_2 (
  input  in_1,
  input  in_2,
  input  in_3,
  output out_4,
  output out_5
);

  wire and_1_out, and_2_out, xor_1_out, xor_2_out;

  xor xor_1 (xor_1_out, in_1, in_2);
  and and_1 (and_1_out, in_1, in_2);
  xor xor_2 (xor_2_out, in_1, in_2);
  and and_2 (and_2_out, xor_1_out, in_3);
  xor xor_3 (out_4, xor_2_out, in_3);
  or or_1 (out_5, and_2_out, and_1_out);
endmodule
