// Logisim project Logisim_fibonacci2.circ as structural Verilog: 8 circuits, main circuit main
module main (
  input  [31:0] \input ,
  output [31:0] \output 
);

  wire freeze, n_low;

  \计数逻辑  \u_计数逻辑  (.\input (\input ), .in_2(1'b0), .n_low(n_low), .freeze(freeze));
  \计算逻辑  \u_计算逻辑  (.in_1(n_low), .in_2(freeze), .in_3(1'b0), .out_4(\output ));
endmodule

module \寄存器矩阵  (
  input  [31:0] a11_in,
  input  [31:0] a12_in,
  input  [31:0] a21_in,
  input  [31:0] a22_in,
  input  in_5,
  input  in_6,
  input  in_7,
  output [31:0] a11_out,
  output [31:0] a12_out,
  output [31:0] a21_out,
  output [31:0] a22_out
);

  Register #(.width(32)) a11 (.D(a11_in), .en(in_5), .Q(a11_out), .clk(in_6), .clr(in_7));
  Register #(.width(32)) a21 (.D(a21_in), .en(in_5), .Q(a21_out), .clk(in_6), .clr(in_7));
  Register #(.width(32)) a12 (.D(a12_in), .en(in_5), .Q(a12_out), .clk(in_6), .clr(in_7));
  Register #(.width(32)) a22 (.D(a22_in), .en(in_5), .Q(a22_out), .clk(in_6), .clr(in_7));

  // Other names for the same wires on the sheet: clk = in_6; clr = in_7; ena = in_5
endmodule

module \矩阵乘法  (
  input  [31:0] a11,
  input  [31:0] a12,
  input  [31:0] a21,
  input  [31:0] a22,
  input  [31:0] b11,
  input  [31:0] b12,
  input  [31:0] b21,
  input  [31:0] b22,
  output [31:0] c11,
  output [31:0] c12,
  output [31:0] c21,
  output [31:0] c22
);

  wire [31:0] multiplier_1_out, multiplier_2_out, multiplier_3_out, multiplier_4_out, multiplier_5_out,
       multiplier_6_out, multiplier_7_out, multiplier_8_out;

  Multiplier #(.width(32)) multiplier_1 (.a(a11), .b(b11), .out(multiplier_1_out));  // open: cin, cout
  Multiplier #(.width(32)) multiplier_2 (.a(a12), .b(b21), .out(multiplier_2_out));  // open: cin, cout
  Multiplier #(.width(32)) multiplier_3 (.a(a11), .b(b12), .out(multiplier_3_out));  // open: cin, cout
  Multiplier #(.width(32)) multiplier_4 (.a(a12), .b(b22), .out(multiplier_4_out));  // open: cin, cout
  Multiplier #(.width(32)) multiplier_5 (.a(a21), .b(b11), .out(multiplier_5_out));  // open: cin, cout
  Multiplier #(.width(32)) multiplier_6 (.a(a22), .b(b21), .out(multiplier_6_out));  // open: cin, cout
  Multiplier #(.width(32)) multiplier_7 (.a(a21), .b(b12), .out(multiplier_7_out));  // open: cin, cout
  Multiplier #(.width(32)) multiplier_8 (.a(a22), .b(b22), .out(multiplier_8_out));  // open: cin, cout
  Adder #(.width(32)) adder_1 (.a(multiplier_1_out), .b(multiplier_2_out), .out(c11));  // open: cin, cout
  Adder #(.width(32)) adder_2 (.a(multiplier_3_out), .b(multiplier_4_out), .out(c12));  // open: cin, cout
  Adder #(.width(32)) adder_3 (.a(multiplier_5_out), .b(multiplier_6_out), .out(c21));  // open: cin, cout
  Adder #(.width(32)) adder_4 (.a(multiplier_7_out), .b(multiplier_8_out), .out(c22));  // open: cin, cout
endmodule

module \矩阵MUX  (
  input  [31:0] a11,
  input  [31:0] a12,
  input  [31:0] a21,
  input  [31:0] a22,
  input  [31:0] b11,
  input  [31:0] b12,
  input  [31:0] b21,
  input  [31:0] b22,
  input  select,
  output [31:0] out11,
  output [31:0] out12,
  output [31:0] out21,
  output [31:0] out22
);

  Multiplexer #(.width(32)) multiplexer_1 (.in0(a11), .in1(b11), .out(out11), .sel(select));  // open: en
  Multiplexer #(.width(32)) multiplexer_2 (.in0(a12), .in1(b12), .out(out12), .sel(select));  // open: en
  Multiplexer #(.width(32)) multiplexer_3 (.in0(a21), .in1(b21), .out(out21), .sel(select));  // open: en
  Multiplexer #(.width(32)) multiplexer_4 (.in0(a22), .in1(b22), .out(out22), .sel(select));  // open: en
endmodule

module \矩阵初始值  (
  output [31:0] out11,
  output [31:0] out12,
  output [31:0] out21,
  output [31:0] out22
);


  assign out11 = 32'h1;
  assign out12 = 32'h1;
  assign out21 = 32'h1;
  assign out22 = {32{1'b0}};
endmodule

module \单位阵  (
  output [31:0] out11,
  output [31:0] out12,
  output [31:0] out21,
  output [31:0] out22
);


  assign out11 = 32'h1;
  assign out12 = {32{1'b0}};
  assign out21 = {32{1'b0}};
  assign out22 = 32'h1;
endmodule

module \计算逻辑  (
  input  in_1,
  input  in_2,
  input  in_3,
  output [31:0] out_4
);

  wire clk, ena, init;
  wire [31:0] a11, a12, a21, a22, s11, s12, s21, s22, \单位阵_1_out11 , \单位阵_1_out12 , \单位阵_1_out21 ,
       \单位阵_1_out22 , \单位阵_2_out11 , \单位阵_2_out12 , \单位阵_2_out21 , \单位阵_2_out22 , \矩阵mux_1_out11 ,
       \矩阵mux_1_out12 , \矩阵mux_1_out21 , \矩阵mux_1_out22 , \矩阵mux_2_out11 , \矩阵mux_2_out12 , \矩阵mux_2_out21 ,
       \矩阵mux_2_out22 , \矩阵mux_3_out11 , \矩阵mux_3_out12 , \矩阵mux_3_out21 , \矩阵mux_3_out22 , \矩阵乘法_1_c11 ,
       \矩阵乘法_1_c12 , \矩阵乘法_1_c21 , \矩阵乘法_1_c22 , \矩阵乘法_2_c11 , \矩阵乘法_2_c12 , \矩阵乘法_2_c21 , \矩阵乘法_2_c22 ,
       \矩阵初始值_1_out11 , \矩阵初始值_1_out12 , \矩阵初始值_1_out21 , \矩阵初始值_1_out22 ;

  Counter #(.width(1), .max('h1), .ongoal("stay")) counter_1 (
    .Q(init), .clk(clk), .clr(in_3));  // open: load, D, count, carry
  Clock clock_1 (.out(clk));
  \单位阵  \u_单位阵_1  (.out11(\单位阵_1_out11 ), .out12(\单位阵_1_out12 ), .out21(\单位阵_1_out21 ), .out22(\单位阵_1_out22 ));
  \矩阵MUX  \u_矩阵mux_1  (
    .a11(\单位阵_1_out11 ), .a12(\单位阵_1_out12 ), .a21(\单位阵_1_out21 ), .a22(\单位阵_1_out22 ), .b11(a11), .b12(a12),
    .b21(a21), .b22(a22), .select(in_1), .out11(\矩阵mux_1_out11 ), .out12(\矩阵mux_1_out12 ),
    .out21(\矩阵mux_1_out21 ), .out22(\矩阵mux_1_out22 ));
  \矩阵乘法  \u_矩阵乘法_1  (
    .a11(a11), .a12(a12), .a21(a21), .a22(a22), .b11(a11), .b12(a12), .b21(a21), .b22(a22),
    .c11(\矩阵乘法_1_c11 ), .c12(\矩阵乘法_1_c12 ), .c21(\矩阵乘法_1_c21 ), .c22(\矩阵乘法_1_c22 ));
  \单位阵  \u_单位阵_2  (.out11(\单位阵_2_out11 ), .out12(\单位阵_2_out12 ), .out21(\单位阵_2_out21 ), .out22(\单位阵_2_out22 ));
  \矩阵乘法  \u_矩阵乘法_2  (
    .a11(s11), .a12(s12), .a21(s21), .a22(s22), .b11(\矩阵mux_1_out11 ), .b12(\矩阵mux_1_out12 ),
    .b21(\矩阵mux_1_out21 ), .b22(\矩阵mux_1_out22 ), .c11(\矩阵乘法_2_c11 ), .c12(\矩阵乘法_2_c12 ), .c21(\矩阵乘法_2_c21 ),
    .c22(\矩阵乘法_2_c22 ));
  \矩阵初始值  \u_矩阵初始值_1  (
    .out11(\矩阵初始值_1_out11 ), .out12(\矩阵初始值_1_out12 ), .out21(\矩阵初始值_1_out21 ), .out22(\矩阵初始值_1_out22 ));
  \矩阵MUX  \u_矩阵mux_2  (
    .a11(\矩阵初始值_1_out11 ), .a12(\矩阵初始值_1_out12 ), .a21(\矩阵初始值_1_out21 ), .a22(\矩阵初始值_1_out22 ),
    .b11(\矩阵乘法_1_c11 ), .b12(\矩阵乘法_1_c12 ), .b21(\矩阵乘法_1_c21 ), .b22(\矩阵乘法_1_c22 ), .select(init),
    .out11(\矩阵mux_2_out11 ), .out12(\矩阵mux_2_out12 ), .out21(\矩阵mux_2_out21 ), .out22(\矩阵mux_2_out22 ));
  not not_1 (ena, in_2);
  \矩阵MUX  \u_矩阵mux_3  (
    .a11(\单位阵_2_out11 ), .a12(\单位阵_2_out12 ), .a21(\单位阵_2_out21 ), .a22(\单位阵_2_out22 ), .b11(\矩阵乘法_2_c11 ),
    .b12(\矩阵乘法_2_c12 ), .b21(\矩阵乘法_2_c21 ), .b22(\矩阵乘法_2_c22 ), .select(init), .out11(\矩阵mux_3_out11 ),
    .out12(\矩阵mux_3_out12 ), .out21(\矩阵mux_3_out21 ), .out22(\矩阵mux_3_out22 ));
  \寄存器矩阵  \u_矩阵A  (
    .a11_in(\矩阵mux_2_out11 ), .a12_in(\矩阵mux_2_out12 ), .a21_in(\矩阵mux_2_out21 ), .a22_in(\矩阵mux_2_out22 ),
    .in_5(ena), .in_6(clk), .in_7(in_3), .a11_out(a11), .a12_out(a12), .a21_out(a21), .a22_out(a22));
  \寄存器矩阵  \u_矩阵S  (
    .a11_in(\矩阵mux_3_out11 ), .a12_in(\矩阵mux_3_out12 ), .a21_in(\矩阵mux_3_out21 ), .a22_in(\矩阵mux_3_out22 ),
    .in_5(ena), .in_6(clk), .in_7(in_3), .a11_out(s11), .a12_out(s12), .a21_out(s21), .a22_out(s22));
  Multiplexer #(.width(32)) multiplexer_1 (.in0({32{1'b0}}), .in1(s12), .out(out_4), .sel(in_2));  // open: en

  // Other names for the same wires on the sheet: clr = in_3; freeze = in_2; n_low = in_1
endmodule

module \计数逻辑  (
  input  [31:0] \input ,
  input  in_2,
  output n_low,
  output freeze
);

  wire clk, comparator_1_eq, init;
  wire [31:0] multiplexer_1_out, n, shifter_1_out;

  Counter #(.width(1), .max('h1), .ongoal("stay")) counter_1 (
    .Q(init), .clk(clk), .clr(in_2));  // open: load, D, count, carry
  Clock clock_1 (.out(clk));
  Shifter #(.width(32), .shift("lr")) shifter_1 (.in(n), .\dist (5'b00001), .out(shifter_1_out));
  Comparator #(.width(32)) comparator_1 (.a(n), .b({32{1'b0}}), .eq(comparator_1_eq));  // open: gt, lt
  Multiplexer #(.width(32)) multiplexer_1 (
    .in0(\input ), .in1(shifter_1_out), .out(multiplexer_1_out), .sel(init));  // open: en
  Bit_Extender #(.in_width(32), .out_width(1)) bit_extender_1 (.in(n), .out(n_low));
  Multiplexer multiplexer_2 (.in0(1'b0), .in1(comparator_1_eq), .out(freeze), .sel(init));  // open: en
  Register #(.width(32)) register_1 (.D(multiplexer_1_out), .Q(n), .clk(clk), .clr(in_2));  // open: en

  // Other names for the same wires on the sheet: clr = in_2
endmodule
