// Logisim project Logisim_mod5.circ as structural Verilog: 3 circuits, main circuit mod5
module mod5 (
  input  in_1,
  output out_2,
  output out_3,
  output out_4,
  output out_5,
  output out_6
);

  wire clock_1_out;
  wire [1:0] in_1_s1_prime, register_1_q;

  In u_in_1 (
    .S1(register_1_q[0]), .S0(register_1_q[1]), .In(in_1), .S1_prime(in_1_s1_prime[0]),
    .S0_prime(in_1_s1_prime[1]));
  Register #(.width(2)) register_1 (.D(in_1_s1_prime), .en(1'b1), .Q(register_1_q), .clk(clock_1_out));  // open: clr
  Clock clock_1 (.out(clock_1_out));
  Out out_1 (
    .in_1(in_1_s1_prime[0]), .in_2(in_1_s1_prime[1]), .out_3(out_2), .out_4(out_3), .out_5(out_4),
    .out_6(out_5), .out_7(out_6));
endmodule

module In (
  input  S1,
  input  S0,
  input  In,
  output S1_prime,
  output S0_prime
);


  assign S0_prime = In;
  assign S1_prime = S0;
endmodule

module Out (
  input  in_1,
  input  in_2,
  output out_3,
  output out_4,
  output out_5,
  output out_6,
  output out_7
);

  wire not_1_out, not_2_out;

  not not_1 (not_1_out, in_1);
  not not_2 (not_2_out, in_2);
  and and_1 (out_4, not_1_out, not_2_out);
  and and_2 (out_5, not_1_out, in_2);
  and and_3 (out_6, in_1, in_2);
  and and_4 (out_7, in_1, not_2_out);

  assign out_3 = 1'b0;
endmodule
