// Logisim project Logisim_swap.circ as structural Verilog: 1 circuit, main circuit swap
// a
module swap (
  input  I1,
  input  I2,
  input  S,
  output _01,
  output _02
);

  wire and_1_out, and_2_out, and_3_out, and_4_out, not_1_out, not_2_out;

  not not_1 (not_1_out, S);
  not not_2 (not_2_out, S);
  // Probe on and_1_out
  and and_1 (and_1_out, I1, S);
  // Probe on and_2_out
  and and_2 (and_2_out, I2, not_1_out);
  // Probe on and_3_out
  and and_3 (and_3_out, I2, S);
  // Probe on and_4_out
  and and_4 (and_4_out, I1, not_2_out);
  or or_1 (_01, and_3_out, and_4_out);
  or or_2 (_02, and_1_out, and_2_out);
endmodule
